// Logisim project master.circ as structural Verilog: 16 circuits, main circuit main
module main (
);

  wire alumicrocoded_1_fc, alumicrocoded_1_fo, alumicrocoded_1_fs, alumicrocoded_1_fz, clock_1_out,
       clock_2_out, clock_3_out, clock_4_out, clock_5_out, clock_6_out, clock_7_out, control_1_mask_restore,
       control_1_mask_save, control_1_oregwe, io_1_ogpu_clear, io_1_okeyread, keyboard_1_avail,
       memory_controller_1_gpu_we, registerfile_1_busy, registerfile_1_int;
  wire [1:0] control_1_oioop;
  wire [2:0] control_1_oioaddr, control_1_omemop, registerfile_1_int_id;
  wire [3:0] control_1_oaluop, control_1_oregid;
  wire [6:0] keyboard_1_data, memory_controller_1_gpu_data;
  wire [7:0] io_1_obusyassert, io_1_ointasssert;
  wire [15:0] alumicrocoded_1_dout, control_1_oiobus, control_1_oregbus, io_1_oled,
       memory_controller_1_databusout;
  wire [15:7] memory_controller_1_gpu_data_2;

  Clock clock_1 (.out(clock_1_out));
  TTY tty_1 (
    .data(memory_controller_1_gpu_data), .clk(clock_1_out), .we(memory_controller_1_gpu_we),
    .clr(io_1_ogpu_clear));
  memory_controller memory_controller_1 (
    .MODE(control_1_omemop), .DataBUSin(memory_controller_1_databusout), .CLK(clock_2_out),
    .GPU_DATA({memory_controller_1_gpu_data_2, memory_controller_1_gpu_data}),
    .GPU_WE(memory_controller_1_gpu_we), .DataBUSout(memory_controller_1_databusout));  // open: GPU_ADDR
  Clock clock_2 (.out(clock_2_out));
  Clock clock_3 (.out(clock_3_out));
  Clock clock_4 (.out(clock_4_out));
  aluMICROCODED alumicrocoded_1 (
    .OP(control_1_oaluop), .CLK(clock_4_out), .Din(alumicrocoded_1_dout), .Dout(alumicrocoded_1_dout),
    .FS(alumicrocoded_1_fs), .FO(alumicrocoded_1_fo), .FC(alumicrocoded_1_fc), .FZ(alumicrocoded_1_fz));
  control control_1 (
    .ialubus(alumicrocoded_1_dout), .ifs(alumicrocoded_1_fs), .ifo(alumicrocoded_1_fo),
    .ifc(alumicrocoded_1_fc), .ifz(alumicrocoded_1_fz), .imembus(memory_controller_1_databusout),
    .iregbus(control_1_oregbus), .iint(registerfile_1_int), .iintid(registerfile_1_int_id),
    .ibusy(registerfile_1_busy), .iiobus(control_1_oiobus), .CLK(clock_3_out), .oregwe(control_1_oregwe),
    .omemop(control_1_omemop), .oioaddr(control_1_oioaddr), .oaluop(control_1_oaluop),
    .oalubus(alumicrocoded_1_dout), .omembus(memory_controller_1_databusout), .oregbus(control_1_oregbus),
    .oregid(control_1_oregid), .mask_save(control_1_mask_save), .mask_restore(control_1_mask_restore),
    .oioop(control_1_oioop), .oiobus(control_1_oiobus));
  IO io_1 (
    .ikeychar(keyboard_1_data), .ikeyaval(keyboard_1_avail), .CLK(clock_7_out), .iioid(control_1_oioaddr),
    .iiocmd(control_1_oioop), .iiobus(control_1_oiobus), .obusyassert(io_1_obusyassert),
    .ogpu_clear(io_1_ogpu_clear), .okeyread(io_1_okeyread), .oled(io_1_oled), .oiobus(control_1_oiobus),
    .ointasssert(io_1_ointasssert));
  Clock clock_5 (.out(clock_5_out));
  Keyboard keyboard_1 (
    .clk(clock_5_out), .re(io_1_okeyread), .clr(1'b0), .avail(keyboard_1_avail), .data(keyboard_1_data));
  Clock clock_6 (.out(clock_6_out));
  Clock clock_7 (.out(clock_7_out));
  registerfile registerfile_1 (
    .regid(control_1_oregid), .mask_restore(control_1_mask_restore), .CLK(clock_6_out),
    .wr_enable(control_1_oregwe), .mask_save(control_1_mask_save), .data_in(control_1_oregbus),
    .ioint(io_1_ointasssert), .iobusy(io_1_obusyassert), .INT_ID(registerfile_1_int_id),
    .INT(registerfile_1_int), .BUSY(registerfile_1_busy), .data_out(control_1_oregbus));
  // LedBar #(.inputtype("row"), .matrixcols(16)) ledbar_1: pin names not known; wires that end beside it: io_1_oled
endmodule

module memory_controller (
  input  [15:0] DataBUSin,
  input  [2:0] MODE,
  input  CLK,
  output [14:0] GPU_ADDR,
  output [15:0] GPU_DATA,
  output GPU_WE,
  output [15:0] DataBUSout
);

  wire and_3_out, not_1_out, output_enable, write_enable;
  wire [15:0] adder_1_out, general_purpose_memory_dout, multiplexer_1_out, multiplexer_2_out, rom_1_data;
  wire [15:15] RegAddr_q;

  not not_1 (not_1_out, output_enable);
  assign GPU_DATA = not_1_out ? DataBUSin : 16'bz;  // Controlled_Buffer controlled_buffer_1
  and and_1 (write_enable, MODE[2], ~MODE[1], ~MODE[0]);  // AND_Gate
  and and_2 (output_enable, MODE[2], MODE[0]);
  Multiplexer #(.width(16)) multiplexer_1 (.in0(GPU_DATA), .in1(adder_1_out), .out(multiplexer_1_out), .sel(MODE[0]));
  Register #(.width(16)) RegAddr (
    .D(multiplexer_1_out), .en(MODE[1]), .clk(CLK), .Q({RegAddr_q[15], GPU_ADDR}));  // open: clr
  Adder #(.width(16)) adder_1 (.a({RegAddr_q[15], GPU_ADDR}), .b(16'h1), .out(adder_1_out));  // open: cin, cout
  and and_3 (and_3_out, RegAddr_q[15], write_enable);
  ROM #(.addrWidth(16), .dataWidth(16)) rom_1 (.addr({RegAddr_q[15], GPU_ADDR}), .data(rom_1_data));
  RAM #(.addrWidth(16), .asyncread("true"), .dataWidth(16), .\type ("nonvolatile")) general_purpose_memory (
    .addr({RegAddr_q[15], GPU_ADDR}), .we(and_3_out), .oe(1'b1), .clk(CLK), .din(GPU_DATA),
    .dout(general_purpose_memory_dout));
  and and_4 (GPU_WE, ~RegAddr_q[15], write_enable);  // AND_Gate
  Multiplexer #(.width(16)) multiplexer_2 (
    .in0(rom_1_data), .in1(general_purpose_memory_dout), .out(multiplexer_2_out), .sel(RegAddr_q[15]));
  assign DataBUSout = output_enable ? multiplexer_2_out : 16'bz;  // Controlled_Buffer controlled_buffer_2

  // Other names for the same wires on the sheet: Data_in[15:0] = GPU_DATA

  // Notes on the sheet:
  //   15 bit
  //   contents of rom_1 (hex, n*v repeats v):
  //   4800 ee c008 6080 8880 fecf 2880 1 9880 fecf d080 b100 c004 c005 c008 c009 c00a 6140 8850 feff 1084
  //   a800 50 3940 a 4900 30 3940 8 4900 3e 9045 2850 1 3950 fff0 4e00 28 1850 ff00 9850 feff d0a0 d090
  //   d080 d050 d040 b100 1850 ff00 9850 feff 1880 1 9880 fefe d0a0 d090 d080 d050 d040 b100 3950 ff00
  //   4900 49 2950 1 1840 20 9045 9850 feff d0a0 d090 d080 d050 d040 b100 0 8890 feef 3980 a 4900 62 3980
  //   8 4900 69 9089 2890 1 2a90 7fff 9890 feef b000 2890 100 2a90 7f00 9890 feef b000 2990 1 2a90 7fff
  //   9890 feef 1880 20 9089 b000 3299 4900 83 c008 c009 8088 a800 50 d090 d080 2880 1 2990 1 4800 73 b000
  //   a800 73 1880 a 4800 50 c004 1048 1880 78 a800 50 1084 2f80 c 2a80 f 2880 fed0 8088 a800 50 1084 2f80
  //   8 2a80 f 2880 fed0 8088 a800 50 1084 2f80 4 2a80 f 2880 fed0 8088 a800 50 1084 2f80 0 2a80 f 2880
  //   fed0 8088 a800 50 d040 b000 3288 4900 c4 1880 f000 1890 4 a800 73 b000 1880 f004 1890 5 a800 73 b000
  //   1880 7fff 1890 20 9098 2980 1 4a00 cf 9098 9880 feef b000 32aa 4900 e8 80b8 80c9 31bc 4a00 eb 2880 1
  //   2890 1 29a0 1 4800 d8 1880 1 b000 1880 0 b000 1820 f000 1880 f009 1890 b a800 84 2b10 8000 2b10 4000
  //   1880 3e a800 50 1880 20 9880 ff00 9880 ff01 9880 ff02 9880 ff03 9880 ff04 9880 ff05 9880 ff06 9880
  //   ff07 9880 ff08 9880 ff09 9880 ff0a 9880 ff0b 9880 ff0c 9880 ff0d 9880 ff0e 9880 ff0f 9880 ff10 9880
  //   ff11 9880 ff12 9880 ff13 9880 ff14 9880 ff15 9880 ff16 9880 ff17 9880 ff18 9880 ff19 9880 ff1a 9880
  //   ff1b 9880 ff1c 9880 ff1d 9880 ff1e 9880 ff1f 9880 ff20 9880 ff21 9880 ff22 9880 ff23 9880 ff24 9880
  //   ff25 9880 ff26 9880 ff27 9880 ff28 9880 ff29 9880 ff2a 9880 ff2b 9880 ff2c 9880 ff2d 9880 ff2e 9880
  //   ff2f 9880 ff30 9880 ff31 9880 ff32 9880 ff33 9880 ff34 9880 ff35 9880 ff36 9880 ff37 9880 ff38 9880
  //   ff39 9880 ff3a 9880 ff3b 9880 ff3c 9880 ff3d 9880 ff3e 9880 ff3f 9880 ff40 9880 ff41 9880 ff42 9880
  //   ff43 9880 ff44 9880 ff45 9880 ff46 9880 ff47 9880 ff48 9880 ff49 9880 ff4a 9880 ff4b 9880 ff4c 9880
  //   ff4d 9880 ff4e 9880 ff4f 9880 ff50 9880 ff51 9880 ff52 9880 ff53 9880 ff54 9880 ff55 9880 ff56 9880
  //   ff57 9880 ff58 9880 ff59 9880 ff5a 9880 ff5b 9880 ff5c 9880 ff5d 9880 ff5e 9880 ff5f 9880 ff60 9880
  //   ff61 9880 ff62 9880 ff63 9880 ff64 9880 ff65 9880 ff66 9880 ff67 9880 ff68 9880 ff69 9880 ff6a 9880
  //   ff6b 9880 ff6c 9880 ff6d 9880 ff6e 9880 ff6f 9880 ff70 9880 ff71 9880 ff72 9880 ff73 9880 ff74 9880
  //   ff75 9880 ff76 9880 ff77 9880 ff78 9880 ff79 9880 ff7a 9880 ff7b 9880 ff7c 9880 ff7d 9880 ff7e 9880
  //   ff7f 9880 ff80 9880 ff81 9880 ff82 9880 ff83 9880 ff84 9880 ff85 9880 ff86 9880 ff87 9880 ff88 9880
  //   ff89 9880 ff8a 9880 ff8b 9880 ff8c 9880 ff8d 9880 ff8e 9880 ff8f 9880 ff90 9880 ff91 9880 ff92 9880
  //   ff93 9880 ff94 9880 ff95 9880 ff96 9880 ff97 9880 ff98 9880 ff99 9880 ff9a 9880 ff9b 9880 ff9c 9880
  //   ff9d 9880 ff9e 9880 ff9f 9880 ffa0 9880 ffa1 9880 ffa2 9880 ffa3 9880 ffa4 9880 ffa5 9880 ffa6 9880
  //   ffa7 9880 ffa8 9880 ffa9 9880 ffaa 9880 ffab 9880 ffac 9880 ffad 9880 ffae 9880 ffaf 9880 ffb0 9880
  //   ffb1 9880 ffb2 9880 ffb3 9880 ffb4 9880 ffb5 9880 ffb6 9880 ffb7 9880 ffb8 9880 ffb9 9880 ffba 9880
  //   ffbb 9880 ffbc 9880 ffbd 9880 ffbe 9880 ffbf 9880 ffc0 9880 ffc1 9880 ffc2 9880 ffc3 9880 ffc4 9880
  //   ffc5 9880 ffc6 9880 ffc7 9880 ffc8 9880 ffc9 9880 ffca 9880 ffcb 9880 ffcc 9880 ffcd 9880 ffce 9880
  //   ffcf 9880 ffd0 9880 ffd1 9880 ffd2 9880 ffd3 9880 ffd4 9880 ffd5 9880 ffd6 9880 ffd7 9880 ffd8 9880
  //   ffd9 9880 ffda 9880 ffdb 9880 ffdc 9880 ffdd 9880 ffde 9880 ffdf 9880 ffe0 9880 ffe1 9880 ffe2 9880
  //   ffe3 9880 ffe4 9880 ffe5 9880 ffe6 9880 ffe7 9880 ffe8 9880 ffe9 9880 ffea 9880 ffeb 9880 ffec 9880
  //   ffed 9880 ffee 9880 ffef 8840 fefe 3244 4900 2e0 1840 0 9840 fefe 1880 ff00 1890 f018 18a0 4 a800 d8
  //   3288 4a00 31d 1880 ff00 1890 f084 18a0 4 a800 d8 3288 4a00 325 1880 ff00 1890 f014 18a0 4 a800 d8
  //   3288 4a00 32d 1880 ff00 1890 f088 18a0 5 a800 d8 3288 4a00 337 1880 f08d 1890 f a800 84 4800 fa 1880
  //   f01c 1890 68 a800 84 4800 fa 1880 ff05 1890 fa a800 84 4800 fa 8880 fecf a800 8a 1880 a a800 50 4800
  //   fa a800 cb 4800 fa 60613*0 74 72 75 65 66 61 6c 73 65 6d 41 4c 55 73 68 20 76 30 2e 31 74 69 6d 65
  //   68 65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
  //   VRAM
  //   ROM
  //   RAM
endmodule

module control (
  input  CLK,
  input  [15:0] ialubus,
  input  ifs,
  input  ifo,
  input  ifc,
  input  ifz,
  input  [15:0] imembus,
  input  [15:0] iregbus,
  input  iint,
  input  [2:0] iintid,
  input  ibusy,
  input  [15:0] iiobus,
  output [3:0] oaluop,
  output [15:0] oalubus,
  output [2:0] omemop,
  output [15:0] omembus,
  output oregwe,
  output [15:0] oregbus,
  output [3:0] oregid,
  output mask_save,
  output mask_restore,
  output [1:0] oioop,
  output [15:0] oiobus,
  output [2:0] oioaddr
);

  wire and_1_out, and_2_out, and_3_out, and_4_out, and_5_out, and_8_out, c, flwe, instr_load, isimm, isint,
       isjump, isret, isstack, next_instr, not_1_out, not_2_out, not_3_out, not_4_out, not_5_out, not_6_out,
       o, or_1_out, or_2_out, or_3_out, regds, regsrc, s, should_jump, tempregwe, valid, xnor_1_out,
       xnor_2_out, xor_1_out, xor_2_out, z;
  wire [1:0] alumode, alusrc, memsrc;
  wire [2:0] intid_saved;
  wire [3:0] adder_2_out, cycle, flags_saved, multiplexer_5_out, multiplexer_8_out, multiplexer_9_out,
       multiplexer_10_out, opcode;
  wire [7:0] instruction_q;
  wire [15:0] alubus, alubuswrite, iobuswrite, ip, ipnext, membus, membuswrite, multiplexer_1_out,
       multiplexer_2_out, multiplexer_3_out, multiplexer_4_out, multiplexer_11_out, multiplexer_16_out,
       regbuswrite, srctempbus, tempreg;
  wire [23:22] rom_1_data;

  Adder #(.width(16)) adder_1 (.a(ip), .b(16'h1), .out(ipnext), .cin(isimm));  // open: cout
  Multiplexer #(.width(16)) multiplexer_1 (.in0(ipnext), .in1(iobuswrite), .out(multiplexer_1_out), .sel(and_1_out));
  and and_1 (and_1_out, isjump, should_jump);
  not not_1 (not_1_out, oaluop[3]);
  assign alubus = not_1_out ? ialubus : 16'bz;  // Controlled_Buffer controlled_buffer_1
  assign membus = and_5_out ? imembus : 16'bz;  // Controlled_Buffer controlled_buffer_2
  Multiplexer #(.width(16)) multiplexer_2 (.in0(membus), .in1({16{1'b0}}), .out(multiplexer_2_out), .sel(isint));
  Multiplexer #(.width(16)) multiplexer_3 (.in0(multiplexer_1_out), .in1(membus), .out(multiplexer_3_out), .sel(isret));
  Multiplexer #(.width(16)) multiplexer_4 (
    .in0(multiplexer_3_out), .in1({{12{1'b1}}, intid_saved, 1'b0}), .out(multiplexer_4_out), .sel(isint));
  Register #(.width(16)) instruction (
    .D(multiplexer_2_out), .en(instr_load), .clk(CLK), .Q({opcode, isimm, oioaddr, instruction_q}), .clr(1'b0));
  Register #(.width(16)) u_IP (.D(multiplexer_4_out), .en(next_instr), .clk(CLK), .Q(ip), .clr(1'b0));
  xnor xnor_1 (xnor_1_out, s, o);
  xor xor_1 (xor_1_out, s, o);
  xnor xnor_2 (xnor_2_out, s, o);
  xor xor_2 (xor_2_out, s, o);
  Clock clock_1 ();  // open: out
  and and_2 (and_2_out, oioop[0], oioop[1]);
  Pull_Resistor pull_resistor_1 (.node({opcode, isimm, oioaddr, instruction_q}));
  not not_2 (not_2_out, z);
  or or_1 (or_1_out, z, xor_1_out);
  and and_3 (and_3_out, ~z, xnor_2_out);  // AND_Gate
  not not_3 (not_3_out, s);
  not not_4 (not_4_out, c);
  or or_2 (or_2_out, c, z);
  and and_4 (and_4_out, ~c, ~z);  // AND_Gate
  not not_5 (not_5_out, o);
  assign oalubus = oaluop[3] ? alubuswrite : 16'bz;  // Controlled_Buffer controlled_buffer_3
  and and_5 (and_5_out, omemop[0], omemop[2]);
  not not_6 (not_6_out, and_5_out);
  assign omembus = not_6_out ? membuswrite : 16'bz;  // Controlled_Buffer controlled_buffer_4
  assign oregbus = oregwe ? regbuswrite : 16'bz;  // Controlled_Buffer controlled_buffer_5
  assign oiobus = and_2_out ? iobuswrite : 16'bz;  // Controlled_Buffer controlled_buffer_6
  Multiplexer #(.width(4)) multiplexer_5 (
    .in0(instruction_q[7:4]), .in1(instruction_q[3:0]), .out(multiplexer_5_out), .sel(regds));
  Multiplexer #(.select(4)) multiplexer_6 (
    .in0(1'b1), .in1(z), .in2(not_2_out), .in3(xnor_1_out), .in4(or_1_out), .in5(and_3_out), .in6(xor_2_out),
    .in7(o), .in8(ibusy), .in9(s), .in10(not_3_out), .in11(not_4_out), .in12(or_2_out), .in13(and_4_out),
    .in14(c), .in15(not_5_out), .out(should_jump), .sel({opcode[0], oioaddr}));
  Multiplexer #(.width(4)) multiplexer_7 (.in0(multiplexer_5_out), .in1(4'b0010), .out(oregid), .sel(isstack));
  Adder #(.width(4)) adder_2 (.a(cycle), .b(4'b0001), .out(adder_2_out));  // open: cin, cout
  Register #(.width(4)) u_cycle (.D(multiplexer_8_out), .en(1'b1), .clk(CLK), .Q(cycle), .clr(1'b0));
  Multiplexer #(.width(4)) multiplexer_8 (.in0(adder_2_out), .in1(4'b0000), .out(multiplexer_8_out), .sel(next_instr));
  Register #(.width(4)) flags (.D(multiplexer_9_out), .en(or_3_out), .clk(CLK), .Q({z, c, o, s}), .clr(1'b0));
  Multiplexer #(.width(4)) multiplexer_9 (
    .in0({ifz, ifc, ifo, ifs}), .in1(flags_saved), .out(multiplexer_9_out), .sel(mask_restore));
  or or_3 (or_3_out, mask_restore, flwe);
  Register #(.width(16)) u_tempreg (.D(membus), .en(tempregwe), .clk(CLK), .Q(tempreg), .clr(1'b0));
  ROM #(.dataWidth(24)) rom_1 (
    .addr({opcode, cycle}),
    .data({rom_1_data, oioop, isret, isstack, tempregwe, isjump, flwe, omemop, memsrc, instr_load, regsrc, oregwe, regds, alusrc, alumode, valid, next_instr}));
  Pull_Resistor pull_resistor_2 (.node(cycle));
  Multiplexer #(.width(4)) multiplexer_10 (
    .in0({z, c, o, s}), .in1({ifz, ifc, ifo, ifs}), .out(multiplexer_10_out), .sel(flwe));
  Pull_Resistor pull_resistor_3 (.node({rom_1_data, oioop, isret, isstack, tempregwe, isjump, flwe, omemop, memsrc, instr_load, regsrc, oregwe, regds, alusrc, alumode, valid, next_instr}));
  Register #(.width(4)) flags_int (.D(multiplexer_10_out), .en(mask_save), .clk(CLK), .Q(flags_saved), .clr(1'b0));
  Register #(.width(4)) register_1 (
    .D({iint, iintid}), .en(next_instr), .clk(CLK), .Q({isint, intid_saved}), .clr(1'b0));
  Pull_Resistor pull_resistor_4 (.node(iintid));
  and and_6 (mask_save, iint, next_instr);
  and and_7 (mask_restore, isret, next_instr, oioaddr[0]);
  Multiplexer #(.width(16)) multiplexer_11 (.in0(ip), .in1(ipnext), .out(multiplexer_11_out), .sel(isjump));
  Multiplexer #(.width(16)) multiplexer_12 (.in0(iregbus), .in1(membus), .out(iobuswrite), .sel(isimm));
  Multiplexer #(.width(16)) multiplexer_13 (.in0(iregbus), .in1(tempreg), .out(srctempbus), .sel(isimm));
  Multiplexer #(.select(2), .width(4)) multiplexer_14 (
    .in0({1'b0, oioaddr}), .in1({3'b100, regds}), .in2(4'b0000), .in3(4'b0001), .out(oaluop), .sel(alumode));
  Multiplexer #(.select(2), .width(16)) multiplexer_15 (
    .in0(iregbus), .in1(iobuswrite), .in2({16{1'b0}}), .in3(16'h1), .out(alubuswrite), .sel(alusrc));
  Multiplexer #(.width(16)) multiplexer_16 (.in0(alubus), .in1(membus), .out(multiplexer_16_out), .sel(regsrc));
  Multiplexer #(.select(2), .width(16)) multiplexer_17 (
    .in0(iregbus), .in1(iobuswrite), .in2(multiplexer_11_out), .in3(srctempbus), .out(membuswrite),
    .sel(memsrc));
  and and_8 (and_8_out, ~oioop[0], oioop[1]);  // AND_Gate
  Multiplexer #(.width(16)) multiplexer_18 (.in0(multiplexer_16_out), .in1(iiobus), .out(regbuswrite), .sel(and_8_out));

  // Other names for the same wires on the sheet: fs = ifs; fo = ifo; fc = ifc; fz = ifz; regwe = oregwe;
  //   memop[2:0] = omemop; ioop[1:0] = oioop; intid[2:0] = iintid; int = iint; funct[2:0] = oioaddr;
  //   aluop[3:0] = oaluop; busy = ibusy; enter_int = mask_save; iobus[15:0] = iiobus; leave_int = mask_restore;
  //   regbus[15:0] = iregbus; regid[3:0] = oregid; srcbus[15:0] = iobuswrite

  // Notes on the sheet:
  //   MEM
  //   REG
  //   IO
  //   ALU
  //   REGISTERS
  //   JUMPS
  //   contents of rom_1 (hex, n*v repeats v):
  //   2802 7202 40004 25074 4208c 4841 10*1 2802 7202 26 5056 8b 11*1 2802 7202 6 5056 8083 11*1 2802 7202
  //   6 5056 8003 11*1 2802 7202 15043 13*1 2802 7202 15043 13*1 2802 7202 200083 13*1 2802 7202 305043
  //   13*1 2802 7202 25002 2c42 5183 11*1 2802 7202 25002 2c42 4003 11*1 2802 7202 40006 25076 4208e 14802
  //   2802 3002 15103 7*1 2802 7202 42006 76 c508b 11*1 2802 7202 40006 25076 4208e 4c43 10*1 2802 7202
  //   42006 76 4008a 5183 10*1 2802 7202 14*1 2802 7202 14*1
  //   CONTROL SIGNALS
  //   BUSES
endmodule

module alu (
  input  [15:0] A,
  input  [15:0] B,
  input  [2:0] funct,
  output FO,
  output FC,
  output FS,
  output [15:0] Y,
  output FZ
);

  wire add_1_cout, add_1_msbcin, multiplexer_1_out, multiplexer_2_out, nor_1_out, sub_1_cout, sub_1_msbcin,
       xor_1_out;
  wire [3:0] add_1_y, add_1_y_2, add_1_y_3, add_1_y_4, and16b_1_y, and16b_1_y_2, and16b_1_y_3, and16b_1_y_4,
       logicshifter_1_y, logicshifter_1_y_2, logicshifter_1_y_3, logicshifter_1_y_4, not16b_1_y,
       not16b_1_y_2, not16b_1_y_3, not16b_1_y_4, or16b_1_y, or16b_1_y_2, or16b_1_y_3, or16b_1_y_4, sub_1_y,
       sub_1_y_2, sub_1_y_3, sub_1_y_4, xor16b_1_y, xor16b_1_y_2, xor16b_1_y_3, xor16b_1_y_4;
  wire [15:0] logicshifter_1_ry, multiplexer_3_out;

  Hex_Digit_Display #(.decimalPoint("false")) hex_digit_display_1 (.value(add_1_y_4));
  Hex_Digit_Display #(.decimalPoint("false")) hex_digit_display_2 (.value(add_1_y_3));
  Hex_Digit_Display #(.decimalPoint("false")) hex_digit_display_3 (.value(add_1_y_2));
  add add_1 (.A(A), .B(B), .Cout(add_1_cout), .MsbCin(add_1_msbcin), .Y({add_1_y_4, add_1_y_3, add_1_y_2, add_1_y}));
  Hex_Digit_Display #(.decimalPoint("false")) hex_digit_display_4 (.value(add_1_y));
  Multiplexer multiplexer_1 (.in0(add_1_cout), .in1(sub_1_msbcin), .out(multiplexer_1_out), .sel(funct[0]));
  xor xor_1 (xor_1_out, multiplexer_1_out, multiplexer_2_out);
  buf buffer_1 (FO, xor_1_out);
  Hex_Digit_Display #(.decimalPoint("false")) hex_digit_display_5 (.value(sub_1_y_4));
  Multiplexer multiplexer_2 (.in0(add_1_msbcin), .in1(sub_1_cout), .out(multiplexer_2_out), .sel(funct[0]));
  buf buffer_2 (FC, multiplexer_2_out);
  Hex_Digit_Display #(.decimalPoint("false")) hex_digit_display_6 (.value(sub_1_y_2));
  Hex_Digit_Display #(.decimalPoint("false")) hex_digit_display_7 (.value(sub_1_y_3));
  sub sub_1 (.A(A), .B(B), .Y({sub_1_y_4, sub_1_y_3, sub_1_y_2, sub_1_y}), .Cout(sub_1_cout), .MsbCin(sub_1_msbcin));
  buf buffer_3 (FS, multiplexer_3_out[15]);
  Hex_Digit_Display #(.decimalPoint("false")) hex_digit_display_8 (.value(sub_1_y));
  Multiplexer #(.select(3), .width(16)) multiplexer_3 (
    .in0({add_1_y_4, add_1_y_3, add_1_y_2, add_1_y}), .in1({sub_1_y_4, sub_1_y_3, sub_1_y_2, sub_1_y}),
    .in2({and16b_1_y_4, and16b_1_y_3, and16b_1_y_2, and16b_1_y}),
    .in3({or16b_1_y_4, or16b_1_y_3, or16b_1_y_2, or16b_1_y}),
    .in4({xor16b_1_y_4, xor16b_1_y_3, xor16b_1_y_2, xor16b_1_y}),
    .in5({not16b_1_y_4, not16b_1_y_3, not16b_1_y_2, not16b_1_y}),
    .in6({logicshifter_1_y_4, logicshifter_1_y_3, logicshifter_1_y_2, logicshifter_1_y}),
    .in7(logicshifter_1_ry), .out(multiplexer_3_out), .sel(funct));
  assign Y = multiplexer_3_out;  // Buffer buffer_4, 16 bits wide
  Hex_Digit_Display #(.decimalPoint("false")) hex_digit_display_9 (.value(and16b_1_y_4));
  Hex_Digit_Display #(.decimalPoint("false")) hex_digit_display_10 (.value(and16b_1_y_3));
  and16b and16b_1 (.B(B), .A(A), .Y({and16b_1_y_4, and16b_1_y_3, and16b_1_y_2, and16b_1_y}));
  Hex_Digit_Display #(.decimalPoint("false")) hex_digit_display_11 (.value(and16b_1_y_2));
  Hex_Digit_Display #(.decimalPoint("false")) hex_digit_display_12 (.value(and16b_1_y));
  nor nor_1 (nor_1_out, multiplexer_3_out[15], multiplexer_3_out[14], multiplexer_3_out[13], multiplexer_3_out[12], multiplexer_3_out[11], multiplexer_3_out[10], multiplexer_3_out[9], multiplexer_3_out[8], multiplexer_3_out[6], multiplexer_3_out[5], multiplexer_3_out[4], multiplexer_3_out[3], multiplexer_3_out[2], multiplexer_3_out[1], multiplexer_3_out[0], multiplexer_3_out[7]);
  buf buffer_5 (FZ, nor_1_out);
  Hex_Digit_Display #(.decimalPoint("false")) hex_digit_display_13 (.value(or16b_1_y_4));
  Hex_Digit_Display #(.decimalPoint("false")) hex_digit_display_14 (.value(or16b_1_y_3));
  Hex_Digit_Display #(.decimalPoint("false")) hex_digit_display_15 (.value(or16b_1_y_2));
  or16b or16b_1 (.B(B), .A(A), .Y({or16b_1_y_4, or16b_1_y_3, or16b_1_y_2, or16b_1_y}));
  Hex_Digit_Display #(.decimalPoint("false")) hex_digit_display_16 (.value(or16b_1_y));
  Hex_Digit_Display #(.decimalPoint("false")) hex_digit_display_17 (.value(xor16b_1_y_4));
  Hex_Digit_Display #(.decimalPoint("false")) hex_digit_display_18 (.value(xor16b_1_y_3));
  xor16b xor16b_1 (.A(A), .B(B), .Y({xor16b_1_y_4, xor16b_1_y_3, xor16b_1_y_2, xor16b_1_y}));
  Hex_Digit_Display #(.decimalPoint("false")) hex_digit_display_19 (.value(xor16b_1_y_2));
  Hex_Digit_Display #(.decimalPoint("false")) hex_digit_display_20 (.value(xor16b_1_y));
  Hex_Digit_Display #(.decimalPoint("false")) hex_digit_display_21 (.value(not16b_1_y_4));
  Hex_Digit_Display #(.decimalPoint("false")) hex_digit_display_22 (.value(not16b_1_y_3));
  not16b not16b_1 (.B(B), .Y({not16b_1_y_4, not16b_1_y_3, not16b_1_y_2, not16b_1_y}));
  Hex_Digit_Display #(.decimalPoint("false")) hex_digit_display_23 (.value(not16b_1_y_2));
  Hex_Digit_Display #(.decimalPoint("false")) hex_digit_display_24 (.value(not16b_1_y));
  Hex_Digit_Display #(.decimalPoint("false")) hex_digit_display_25 (.value(logicshifter_1_y_4));
  Hex_Digit_Display #(.decimalPoint("false")) hex_digit_display_26 (.value(logicshifter_1_y_3));
  Hex_Digit_Display #(.decimalPoint("false")) hex_digit_display_27 (.value(logicshifter_1_y_2));
  logicshifter logicshifter_1 (
    .B(B), .A(A), .Right(funct[0]),
    .Y({logicshifter_1_y_4, logicshifter_1_y_3, logicshifter_1_y_2, logicshifter_1_y}), .rY(logicshifter_1_ry));
  Hex_Digit_Display #(.decimalPoint("false")) hex_digit_display_28 (.value(logicshifter_1_y));
endmodule

module registerfile (
  input  [7:0] ioint,
  input  CLK,
  input  [15:0] data_in,
  input  [7:0] iobusy,
  input  wr_enable,
  input  mask_save,
  input  mask_restore,
  input  [3:0] regid,
  output [2:0] INT_ID,
  output INT,
  output BUSY,
  output [15:0] data_out
);

  wire demultiplexer_1_out0, demultiplexer_1_out2, demultiplexer_1_out3, demultiplexer_1_out4,
       demultiplexer_1_out5, demultiplexer_1_out6, demultiplexer_1_out7, demultiplexer_1_out8,
       demultiplexer_1_out9, demultiplexer_1_out10, demultiplexer_1_out11, demultiplexer_1_out12,
       demultiplexer_1_out13, demultiplexer_1_out14, demultiplexer_1_out15, not_1_out, or_1_out, r1we;
  wire [7:0] and_1_out;
  wire [15:0] mask_saved, multiplexer_1_out, multiplexer_2_out, multiplexer_3_out, multiplexer_4_out, r0_out,
       r1_out, r2_q, r3_q, r4_q, r5_q, r6_q, r7_q, r8_q, r9_q, r10_q, r11_q, r12_q, r13_q, r14_q, r15_q;

  Demultiplexer #(.select(4)) demultiplexer_1 (
    .out0(demultiplexer_1_out0), .out1(r1we), .out2(demultiplexer_1_out2), .out3(demultiplexer_1_out3),
    .out4(demultiplexer_1_out4), .out5(demultiplexer_1_out5), .out6(demultiplexer_1_out6),
    .out7(demultiplexer_1_out7), .out8(demultiplexer_1_out8), .out9(demultiplexer_1_out9),
    .out10(demultiplexer_1_out10), .out11(demultiplexer_1_out11), .out12(demultiplexer_1_out12),
    .out13(demultiplexer_1_out13), .out14(demultiplexer_1_out14), .out15(demultiplexer_1_out15),
    .in(wr_enable), .sel(regid));
  Multiplexer #(.width(16)) multiplexer_1 (.in0(r1_out), .in1(data_in), .out(multiplexer_1_out), .sel(r1we));
  // NoConnect on demultiplexer_1_out0
  Register #(.width(16)) mask_storage (.D(multiplexer_1_out), .en(mask_save), .clk(CLK), .Q(mask_saved));  // open: clr
  Multiplexer #(.width(16)) multiplexer_2 (
    .in0(data_in), .in1(mask_saved), .out(multiplexer_2_out), .sel(mask_restore));
  Multiplexer #(.width(16)) multiplexer_3 (
    .in0(multiplexer_2_out), .in1({16{1'b0}}), .out(multiplexer_3_out), .sel(mask_save));
  or or_1 (or_1_out, r1we, mask_save, mask_restore);
  Register #(.width(16)) r0 (.D({ioint, iobusy}), .en(1'b1), .clk(CLK), .Q(r0_out));  // open: clr
  Register #(.width(16)) r1 (.D(multiplexer_3_out), .en(or_1_out), .clk(CLK), .Q(r1_out));  // open: clr
  Register #(.width(16)) r2 (.D(data_in), .en(demultiplexer_1_out2), .clk(CLK), .Q(r2_q));  // open: clr
  Register #(.width(16)) r3 (.D(data_in), .en(demultiplexer_1_out3), .clk(CLK), .Q(r3_q));  // open: clr
  Register #(.width(16)) r4 (.D(data_in), .en(demultiplexer_1_out4), .clk(CLK), .Q(r4_q));  // open: clr
  Register #(.width(16)) r5 (.D(data_in), .en(demultiplexer_1_out5), .clk(CLK), .Q(r5_q));  // open: clr
  Register #(.width(16)) r6 (.D(data_in), .en(demultiplexer_1_out6), .clk(CLK), .Q(r6_q));  // open: clr
  Register #(.width(16)) r7 (.D(data_in), .en(demultiplexer_1_out7), .clk(CLK), .Q(r7_q));  // open: clr
  Register #(.width(16)) r8 (.D(data_in), .en(demultiplexer_1_out8), .clk(CLK), .Q(r8_q));  // open: clr
  Register #(.width(16)) r9 (.D(data_in), .en(demultiplexer_1_out9), .clk(CLK), .Q(r9_q));  // open: clr
  Register #(.width(16)) r10 (.D(data_in), .en(demultiplexer_1_out10), .clk(CLK), .Q(r10_q));  // open: clr
  Register #(.width(16)) r11 (.D(data_in), .en(demultiplexer_1_out11), .clk(CLK), .Q(r11_q));  // open: clr
  Register #(.width(16)) r12 (.D(data_in), .en(demultiplexer_1_out12), .clk(CLK), .Q(r12_q));  // open: clr
  Register #(.width(16)) r13 (.D(data_in), .en(demultiplexer_1_out13), .clk(CLK), .Q(r13_q));  // open: clr
  Register #(.width(16)) r14 (.D(data_in), .en(demultiplexer_1_out14), .clk(CLK), .Q(r14_q));  // open: clr
  Register #(.width(16)) r15 (.D(data_in), .en(demultiplexer_1_out15), .clk(CLK), .Q(r15_q));  // open: clr
  assign data_out = not_1_out ? multiplexer_4_out : 16'bz;  // Controlled_Buffer controlled_buffer_1
  Multiplexer #(.select(4), .width(16)) multiplexer_4 (
    .in0(r0_out), .in1(r1_out), .in2(r2_q), .in3(r3_q), .in4(r4_q), .in5(r5_q), .in6(r6_q), .in7(r7_q),
    .in8(r8_q), .in9(r9_q), .in10(r10_q), .in11(r11_q), .in12(r12_q), .in13(r13_q), .in14(r14_q),
    .in15(r15_q), .out(multiplexer_4_out), .sel(regid));
  not not_1 (not_1_out, wr_enable);
  assign and_1_out = r0_out[15:8] & r1_out[15:8];  // AND_Gate and_1, 8 bits wide
  or or_2 (BUSY, r0_out[0], r0_out[1], r0_out[2], r0_out[3], r0_out[4], r0_out[5], r0_out[6], r0_out[7]);
  Priority_Encoder priority_encoder_1 (
    .in0(and_1_out[7]), .in1(and_1_out[6]), .in2(and_1_out[5]), .in3(and_1_out[4]), .in4(and_1_out[3]),
    .in5(and_1_out[2]), .in6(and_1_out[1]), .in7(and_1_out[0]), .out(INT_ID), .gs(INT));  // open: en_in, en_out

  // Other names for the same wires on the sheet: data_tunnel[15:0] = data_in; reg_num[3:0] = regid; we = wr_enable

  // Notes on the sheet:
  //   necessary to prevent incredibely rare situation
  //   when int happens EXACTLY on mask update
endmodule

module IO (
  input  CLK,
  input  [15:0] iiobus,
  input  [2:0] iioid,
  input  [1:0] iiocmd,
  input  [6:0] ikeychar,
  input  ikeyaval,
  output [15:0] oiobus,
  output [7:0] ointasssert,
  output [7:0] obusyassert,
  output ogpu_clear,
  output okeyread,
  output [15:0] oled
);

  wire and_2_out, and_3_out, and_4_out, and_7_out, isclock, isgpu, iskeyboard, isled, or_2_out, re, we;
  wire [6:0] keyoutput;
  wire [7:0] multiplexer_1_out;
  wire [11:0] adder_1_out, register_2_q;
  wire [15:0] multiplexer_2_out;

  or or_1 (okeyread, and_2_out, and_3_out);
  Register register_1 (.D(multiplexer_1_out), .en(okeyread), .clk(CLK), .Q({ointasssert[6], keyoutput}), .clr(1'b0));
  Multiplexer #(.width(8)) multiplexer_1 (
    .in0({8{1'b0}}), .in1({1'b1, ikeychar}), .out(multiplexer_1_out), .sel(ikeyaval));
  Register #(.width(12)) register_2 (.D(adder_1_out), .en(1'b1), .clk(CLK), .Q(register_2_q), .clr(ointasssert[7]));
  Adder #(.width(12)) adder_1 (.a(register_2_q), .b(12'h1), .out(adder_1_out));  // open: cin, cout
  and and_1 (ogpu_clear, isgpu, we);
  and and_2 (and_2_out, iskeyboard, re);
  and and_3 (and_3_out, ikeyaval, ~ointasssert[6]);  // AND_Gate
  and and_4 (and_4_out, isled, we);
  and and_5 (we, iiocmd[0], iiocmd[1]);
  and and_6 (re, iiocmd[1], ~iiocmd[0]);  // AND_Gate
  Register #(.width(16)) register_3 (.D(iiobus), .en(and_4_out), .clk(CLK), .Q(oled), .clr(1'b0));
  and and_7 (and_7_out, isclock, re);
  Multiplexer #(.select(3), .width(16)) multiplexer_2 (
    .in0({16{1'b0}}), .in1({{9{1'b0}}, keyoutput}), .in2({16{1'b0}}), .in3({16{1'b0}}), .in4({16{1'b0}}),
    .in5({16{1'b0}}), .in6({16{1'b0}}), .in7({16{1'b0}}), .out(multiplexer_2_out), .sel(iioid));
  or or_2 (or_2_out, and_7_out, register_2_q[11]);
  assign oiobus = re ? multiplexer_2_out : 16'bz;  // Controlled_Buffer controlled_buffer_1
  Register #(.width(1)) register_4 (.D(register_2_q[11]), .en(or_2_out), .clk(CLK), .Q(ointasssert[7]), .clr(1'b0));
  Demultiplexer #(.select(3)) demultiplexer_1 (
    .out0(isclock), .out1(iskeyboard), .out2(isgpu), .out7(isled), .in(1'b1), .sel(iioid));  // open: out3, out4, out5, out6

  assign obusyassert = {8{1'b0}};
  assign ointasssert[5:0] = {6{1'b0}};

  // Other names for the same wires on the sheet: keychar[6:0] = ikeychar; iobus[15:0] = iiobus; ioid[2:0] = iioid;
  //   keyaval = ikeyaval; keyread = okeyread; key_present = ointasssert[6]; clockint = ointasssert[7]

  // Notes on the sheet:
  //   GPU interface
  //   clock
  //   CPU interface
  //   keyboard interface
  //   led interface
  //   IO interface
endmodule

module add (
  input  [15:0] B,
  input  [15:0] A,
  output [15:0] Y,
  output Cout,
  output MsbCin
);

  wire n74283_1_pin9, n74283_2_pin9, n74283_3_pin9;

  fulladd4b fulladd4b_1 (
    .B0(B[12]), .B1(B[13]), .B2(B[14]), .B3(B[15]), .A0(A[12]), .A1(A[13]), .A2(A[14]), .A3(A[15]),
    .Cin(n74283_3_pin9), .MsbCin(MsbCin), .Cout(Cout), .Y0(Y[12]), .Y1(Y[13]), .Y2(Y[14]), .Y3(Y[15]));
  _74283 u_74283_1 (
    .pin1(Y[1]), .pin2(B[1]), .pin3(A[1]), .pin4(Y[0]), .pin5(A[0]), .pin6(B[0]), .pin15(B[2]), .pin14(A[2]),
    .pin13(Y[2]), .pin12(A[3]), .pin11(B[3]), .pin10(Y[3]), .pin9(n74283_1_pin9));  // open: pin7
  _74283 u_74283_2 (
    .pin1(Y[5]), .pin2(B[5]), .pin3(A[5]), .pin4(Y[4]), .pin5(A[4]), .pin6(B[4]), .pin7(n74283_1_pin9),
    .pin15(B[6]), .pin14(A[6]), .pin13(Y[6]), .pin12(A[7]), .pin11(B[7]), .pin10(Y[7]), .pin9(n74283_2_pin9));
  _74283 u_74283_3 (
    .pin1(Y[9]), .pin2(B[9]), .pin3(A[9]), .pin4(Y[8]), .pin5(A[8]), .pin6(B[8]), .pin7(n74283_2_pin9),
    .pin15(B[10]), .pin14(A[10]), .pin13(Y[10]), .pin12(A[11]), .pin11(B[11]), .pin10(Y[11]),
    .pin9(n74283_3_pin9));
endmodule

module sub (
  input  [15:0] A,
  input  [15:0] B,
  output Cout,
  output MsbCin,
  output [15:0] Y
);

  wire n74283_1_pin7, n74283_1_pin9, n74283_2_pin9, n74283_3_pin9;
  wire [15:0] n7404_1_pin2;

  _7404 u_7404_1 (
    .pin1(B[0]), .pin2(n7404_1_pin2[0]), .pin3(B[1]), .pin4(n7404_1_pin2[1]), .pin5(B[2]),
    .pin6(n7404_1_pin2[2]), .pin13(B[8]), .pin12(n7404_1_pin2[8]), .pin11(B[9]), .pin10(n7404_1_pin2[9]),
    .pin9(B[10]), .pin8(n7404_1_pin2[10]));
  _7404 u_7404_2 (
    .pin1(B[3]), .pin2(n7404_1_pin2[3]), .pin3(B[4]), .pin4(n7404_1_pin2[4]), .pin5(B[5]),
    .pin6(n7404_1_pin2[5]), .pin13(B[11]), .pin12(n7404_1_pin2[11]), .pin11(B[12]), .pin10(n7404_1_pin2[12]),
    .pin9(B[13]), .pin8(n7404_1_pin2[13]));
  _7404 u_7404_3 (
    .pin1(B[6]), .pin2(n7404_1_pin2[6]), .pin3(B[7]), .pin4(n7404_1_pin2[7]), .pin13(B[14]),
    .pin12(n7404_1_pin2[14]), .pin11(B[15]), .pin10(n7404_1_pin2[15]));  // open: pin5, pin6, pin9, pin8
  fulladd4b fulladd4b_1 (
    .B0(A[12]), .B1(A[13]), .B2(A[14]), .B3(A[15]), .A0(n7404_1_pin2[12]), .A1(n7404_1_pin2[13]),
    .A2(n7404_1_pin2[14]), .A3(n7404_1_pin2[15]), .Cin(n74283_3_pin9), .MsbCin(MsbCin), .Cout(Cout),
    .Y0(Y[12]), .Y1(Y[13]), .Y2(Y[14]), .Y3(Y[15]));
  _74283 u_74283_1 (
    .pin1(Y[1]), .pin2(n7404_1_pin2[1]), .pin3(A[1]), .pin4(Y[0]), .pin5(A[0]), .pin6(n7404_1_pin2[0]),
    .pin7(n74283_1_pin7), .pin15(n7404_1_pin2[2]), .pin14(A[2]), .pin13(Y[2]), .pin12(A[3]),
    .pin11(n7404_1_pin2[3]), .pin10(Y[3]), .pin9(n74283_1_pin9));
  _74283 u_74283_2 (
    .pin1(Y[5]), .pin2(n7404_1_pin2[5]), .pin3(A[5]), .pin4(Y[4]), .pin5(A[4]), .pin6(n7404_1_pin2[4]),
    .pin7(n74283_1_pin9), .pin15(n7404_1_pin2[6]), .pin14(A[6]), .pin13(Y[6]), .pin12(A[7]),
    .pin11(n7404_1_pin2[7]), .pin10(Y[7]), .pin9(n74283_2_pin9));
  _74283 u_74283_3 (
    .pin1(Y[9]), .pin2(n7404_1_pin2[9]), .pin3(A[9]), .pin4(Y[8]), .pin5(A[8]), .pin6(n7404_1_pin2[8]),
    .pin7(n74283_2_pin9), .pin15(n7404_1_pin2[10]), .pin14(A[10]), .pin13(Y[10]), .pin12(A[11]),
    .pin11(n7404_1_pin2[11]), .pin10(Y[11]), .pin9(n74283_3_pin9));
  // also tied to VCC on the sheet: n74283_1_pin7
endmodule

module fulladd4b (
  input  Cin,
  input  A0,
  input  B0,
  input  A1,
  input  B1,
  input  A2,
  input  B2,
  input  A3,
  input  B3,
  output Y0,
  output Y1,
  output Y2,
  output MsbCin,
  output Cout,
  output Y3
);

  wire n7408_1_pin3, n7408_1_pin6, n7408_1_pin8, n7408_1_pin11, n7408_2_pin3, n7408_2_pin6, n7408_2_pin8,
       n7408_2_pin11, n7486_1_pin3, n7486_1_pin5, n7486_1_pin11, n7486_2_pin3, n7486_2_pin9, n7486_2_pin11;

  _7486 u_7486_1 (
    .pin1(A1), .pin2(B1), .pin3(n7486_1_pin3), .pin4(n7486_1_pin3), .pin5(n7486_1_pin5), .pin6(Y1),
    .pin13(B0), .pin12(A0), .pin11(n7486_1_pin11), .pin10(n7486_1_pin11), .pin9(Cin), .pin8(Y0));
  _7486 u_7486_2 (
    .pin1(A3), .pin2(B3), .pin3(n7486_2_pin3), .pin4(n7486_2_pin3), .pin5(MsbCin), .pin6(Y3), .pin13(B2),
    .pin12(A2), .pin11(n7486_2_pin11), .pin10(n7486_2_pin11), .pin9(n7486_2_pin9), .pin8(Y2));
  _7408 u_7408_1 (
    .pin1(B1), .pin2(A1), .pin3(n7408_1_pin3), .pin4(n7486_1_pin3), .pin5(n7486_1_pin5), .pin6(n7408_1_pin6),
    .pin13(A0), .pin12(B0), .pin11(n7408_1_pin11), .pin10(n7486_1_pin11), .pin9(Cin), .pin8(n7408_1_pin8));
  _7408 u_7408_2 (
    .pin1(B3), .pin2(A3), .pin3(n7408_2_pin3), .pin4(n7486_2_pin3), .pin5(MsbCin), .pin6(n7408_2_pin6),
    .pin13(A2), .pin12(B2), .pin11(n7408_2_pin11), .pin10(n7486_2_pin11), .pin9(n7486_2_pin9),
    .pin8(n7408_2_pin8));
  _7432 u_7432_1 (
    .pin1(n7408_2_pin11), .pin2(n7408_2_pin8), .pin3(MsbCin), .pin4(n7408_2_pin6), .pin5(n7408_2_pin3),
    .pin6(Cout), .pin13(n7408_1_pin8), .pin12(n7408_1_pin11), .pin11(n7486_1_pin5), .pin10(n7408_1_pin6),
    .pin9(n7408_1_pin3), .pin8(n7486_2_pin9));
endmodule

module and16b (
  input  [15:0] A,
  input  [15:0] B,
  output [15:0] Y
);

  _7408 u_7408_1 (
    .pin1(A[2]), .pin2(B[2]), .pin3(Y[2]), .pin4(A[3]), .pin5(B[3]), .pin6(Y[3]), .pin13(A[1]), .pin12(B[1]),
    .pin11(Y[1]), .pin10(A[0]), .pin9(B[0]), .pin8(Y[0]));
  _7408 u_7408_2 (
    .pin1(A[6]), .pin2(B[6]), .pin3(Y[6]), .pin4(A[7]), .pin5(B[7]), .pin6(Y[7]), .pin13(A[5]), .pin12(B[5]),
    .pin11(Y[5]), .pin10(A[4]), .pin9(B[4]), .pin8(Y[4]));
  _7408 u_7408_3 (
    .pin1(A[10]), .pin2(B[10]), .pin3(Y[10]), .pin4(A[11]), .pin5(B[11]), .pin6(Y[11]), .pin13(A[9]),
    .pin12(B[9]), .pin11(Y[9]), .pin10(A[8]), .pin9(B[8]), .pin8(Y[8]));
  _7408 u_7408_4 (
    .pin1(A[14]), .pin2(B[14]), .pin3(Y[14]), .pin4(A[15]), .pin5(B[15]), .pin6(Y[15]), .pin13(A[13]),
    .pin12(B[13]), .pin11(Y[13]), .pin10(A[12]), .pin9(B[12]), .pin8(Y[12]));
endmodule

module or16b (
  input  [15:0] A,
  input  [15:0] B,
  output [15:0] Y
);

  _7432 u_7432_1 (
    .pin1(A[2]), .pin2(B[2]), .pin3(Y[2]), .pin4(A[3]), .pin5(B[3]), .pin6(Y[3]), .pin13(A[1]), .pin12(B[1]),
    .pin11(Y[1]), .pin10(A[0]), .pin9(B[0]), .pin8(Y[0]));
  _7432 u_7432_2 (
    .pin1(A[6]), .pin2(B[6]), .pin3(Y[6]), .pin4(A[7]), .pin5(B[7]), .pin6(Y[7]), .pin13(A[5]), .pin12(B[5]),
    .pin11(Y[5]), .pin10(A[4]), .pin9(B[4]), .pin8(Y[4]));
  _7432 u_7432_3 (
    .pin1(A[10]), .pin2(B[10]), .pin3(Y[10]), .pin4(A[11]), .pin5(B[11]), .pin6(Y[11]), .pin13(A[9]),
    .pin12(B[9]), .pin11(Y[9]), .pin10(A[8]), .pin9(B[8]), .pin8(Y[8]));
  _7432 u_7432_4 (
    .pin1(A[14]), .pin2(B[14]), .pin3(Y[14]), .pin4(A[15]), .pin5(B[15]), .pin6(Y[15]), .pin13(A[13]),
    .pin12(B[13]), .pin11(Y[13]), .pin10(A[12]), .pin9(B[12]), .pin8(Y[12]));
endmodule

module xor16b (
  input  [15:0] A,
  input  [15:0] B,
  output [15:0] Y
);

  _7486 u_7486_1 (
    .pin1(A[2]), .pin2(B[2]), .pin3(Y[2]), .pin4(A[3]), .pin5(B[3]), .pin6(Y[3]), .pin13(A[1]), .pin12(B[1]),
    .pin11(Y[1]), .pin10(A[0]), .pin9(B[0]), .pin8(Y[0]));
  _7486 u_7486_2 (
    .pin1(A[6]), .pin2(B[6]), .pin3(Y[6]), .pin4(A[7]), .pin5(B[7]), .pin6(Y[7]), .pin13(A[5]), .pin12(B[5]),
    .pin11(Y[5]), .pin10(A[4]), .pin9(B[4]), .pin8(Y[4]));
  _7486 u_7486_3 (
    .pin1(A[10]), .pin2(B[10]), .pin3(Y[10]), .pin4(A[11]), .pin5(B[11]), .pin6(Y[11]), .pin13(A[9]),
    .pin12(B[9]), .pin11(Y[9]), .pin10(A[8]), .pin9(B[8]), .pin8(Y[8]));
  _7486 u_7486_4 (
    .pin1(A[14]), .pin2(B[14]), .pin3(Y[14]), .pin4(A[15]), .pin5(B[15]), .pin6(Y[15]), .pin13(A[13]),
    .pin12(B[13]), .pin11(Y[13]), .pin10(A[12]), .pin9(B[12]), .pin8(Y[12]));
endmodule

module not16b (
  input  [15:0] B,
  output [15:0] Y
);

  _7414 u_7414_1 (
    .pin1(B[3]), .pin2(Y[3]), .pin3(B[4]), .pin4(Y[4]), .pin5(B[5]), .pin6(Y[5]), .pin13(B[2]), .pin12(Y[2]),
    .pin11(B[1]), .pin10(Y[1]), .pin9(B[0]), .pin8(Y[0]));
  _7414 u_7414_2 (
    .pin1(B[9]), .pin2(Y[9]), .pin3(B[10]), .pin4(Y[10]), .pin5(B[11]), .pin6(Y[11]), .pin13(B[8]),
    .pin12(Y[8]), .pin11(B[7]), .pin10(Y[7]), .pin9(B[6]), .pin8(Y[6]));
  _7414 u_7414_3 (
    .pin1(B[15]), .pin2(Y[15]), .pin13(B[14]), .pin12(Y[14]), .pin11(B[13]), .pin10(Y[13]), .pin9(B[12]),
    .pin8(Y[12]));  // open: pin3, pin4, pin5, pin6
endmodule

module lsl (
  input  [15:0] B,
  input  [15:0] A,
  output [15:0] Y
);

  wire pull_resistor_1_node;

  Multiplexer #(.select(4)) multiplexer_1 (
    .in0(A[15]), .in1(A[14]), .in2(A[13]), .in3(A[12]), .in4(A[11]), .in5(A[10]), .in6(A[9]), .in7(A[8]),
    .in8(A[7]), .in9(A[6]), .in10(A[5]), .in11(A[4]), .in12(A[3]), .in13(A[2]), .in14(A[1]), .in15(A[0]),
    .out(Y[15]), .sel(B[3:0]));
  Multiplexer #(.select(4)) multiplexer_2 (
    .in0(A[14]), .in1(A[13]), .in2(A[12]), .in3(A[11]), .in4(A[10]), .in5(A[9]), .in6(A[8]), .in7(A[7]),
    .in8(A[6]), .in9(A[5]), .in10(A[4]), .in11(A[3]), .in12(A[2]), .in13(A[1]), .in14(A[0]),
    .in15(pull_resistor_1_node), .out(Y[14]), .sel(B[3:0]));
  Multiplexer #(.select(4)) multiplexer_3 (
    .in0(A[13]), .in1(A[12]), .in2(A[11]), .in3(A[10]), .in4(A[9]), .in5(A[8]), .in6(A[7]), .in7(A[6]),
    .in8(A[5]), .in9(A[4]), .in10(A[3]), .in11(A[2]), .in12(A[1]), .in13(A[0]), .in14(pull_resistor_1_node),
    .in15(pull_resistor_1_node), .out(Y[13]), .sel(B[3:0]));
  Multiplexer #(.select(4)) multiplexer_4 (
    .in0(A[12]), .in1(A[11]), .in2(A[10]), .in3(A[9]), .in4(A[8]), .in5(A[7]), .in6(A[6]), .in7(A[5]),
    .in8(A[4]), .in9(A[3]), .in10(A[2]), .in11(A[1]), .in12(A[0]), .in13(pull_resistor_1_node),
    .in14(pull_resistor_1_node), .in15(pull_resistor_1_node), .out(Y[12]), .sel(B[3:0]));
  Multiplexer #(.select(4)) multiplexer_5 (
    .in0(A[11]), .in1(A[10]), .in2(A[9]), .in3(A[8]), .in4(A[7]), .in5(A[6]), .in6(A[5]), .in7(A[4]),
    .in8(A[3]), .in9(A[2]), .in10(A[1]), .in11(A[0]), .in12(pull_resistor_1_node),
    .in13(pull_resistor_1_node), .in14(pull_resistor_1_node), .in15(pull_resistor_1_node), .out(Y[11]),
    .sel(B[3:0]));
  Multiplexer #(.select(4)) multiplexer_6 (
    .in0(A[10]), .in1(A[9]), .in2(A[8]), .in3(A[7]), .in4(A[6]), .in5(A[5]), .in6(A[4]), .in7(A[3]),
    .in8(A[2]), .in9(A[1]), .in10(A[0]), .in11(pull_resistor_1_node), .in12(pull_resistor_1_node),
    .in13(pull_resistor_1_node), .in14(pull_resistor_1_node), .in15(pull_resistor_1_node), .out(Y[10]),
    .sel(B[3:0]));
  Multiplexer #(.select(4)) multiplexer_7 (
    .in0(A[9]), .in1(A[8]), .in2(A[7]), .in3(A[6]), .in4(A[5]), .in5(A[4]), .in6(A[3]), .in7(A[2]),
    .in8(A[1]), .in9(A[0]), .in10(pull_resistor_1_node), .in11(pull_resistor_1_node),
    .in12(pull_resistor_1_node), .in13(pull_resistor_1_node), .in14(pull_resistor_1_node),
    .in15(pull_resistor_1_node), .out(Y[9]), .sel(B[3:0]));
  Multiplexer #(.select(4)) multiplexer_8 (
    .in0(A[8]), .in1(A[7]), .in2(A[6]), .in3(A[5]), .in4(A[4]), .in5(A[3]), .in6(A[2]), .in7(A[1]),
    .in8(A[0]), .in9(pull_resistor_1_node), .in10(pull_resistor_1_node), .in11(pull_resistor_1_node),
    .in12(pull_resistor_1_node), .in13(pull_resistor_1_node), .in14(pull_resistor_1_node),
    .in15(pull_resistor_1_node), .out(Y[8]), .sel(B[3:0]));
  Multiplexer #(.select(4)) multiplexer_9 (
    .in0(A[7]), .in1(A[6]), .in2(A[5]), .in3(A[4]), .in4(A[3]), .in5(A[2]), .in6(A[1]), .in7(A[0]),
    .in8(pull_resistor_1_node), .in9(pull_resistor_1_node), .in10(pull_resistor_1_node),
    .in11(pull_resistor_1_node), .in12(pull_resistor_1_node), .in13(pull_resistor_1_node),
    .in14(pull_resistor_1_node), .in15(pull_resistor_1_node), .out(Y[7]), .sel(B[3:0]));
  Multiplexer #(.select(4)) multiplexer_10 (
    .in0(A[6]), .in1(A[5]), .in2(A[4]), .in3(A[3]), .in4(A[2]), .in5(A[1]), .in6(A[0]),
    .in7(pull_resistor_1_node), .in8(pull_resistor_1_node), .in9(pull_resistor_1_node),
    .in10(pull_resistor_1_node), .in11(pull_resistor_1_node), .in12(pull_resistor_1_node),
    .in13(pull_resistor_1_node), .in14(pull_resistor_1_node), .in15(pull_resistor_1_node), .out(Y[6]),
    .sel(B[3:0]));
  Multiplexer #(.select(4)) multiplexer_11 (
    .in0(A[5]), .in1(A[4]), .in2(A[3]), .in3(A[2]), .in4(A[1]), .in5(A[0]), .in6(pull_resistor_1_node),
    .in7(pull_resistor_1_node), .in8(pull_resistor_1_node), .in9(pull_resistor_1_node),
    .in10(pull_resistor_1_node), .in11(pull_resistor_1_node), .in12(pull_resistor_1_node),
    .in13(pull_resistor_1_node), .in14(pull_resistor_1_node), .in15(pull_resistor_1_node), .out(Y[5]),
    .sel(B[3:0]));
  Multiplexer #(.select(4)) multiplexer_12 (
    .in0(A[4]), .in1(A[3]), .in2(A[2]), .in3(A[1]), .in4(A[0]), .in5(pull_resistor_1_node),
    .in6(pull_resistor_1_node), .in7(pull_resistor_1_node), .in8(pull_resistor_1_node),
    .in9(pull_resistor_1_node), .in10(pull_resistor_1_node), .in11(pull_resistor_1_node),
    .in12(pull_resistor_1_node), .in13(pull_resistor_1_node), .in14(pull_resistor_1_node),
    .in15(pull_resistor_1_node), .out(Y[4]), .sel(B[3:0]));
  Multiplexer #(.select(4)) multiplexer_13 (
    .in0(A[3]), .in1(A[2]), .in2(A[1]), .in3(A[0]), .in4(pull_resistor_1_node), .in5(pull_resistor_1_node),
    .in6(pull_resistor_1_node), .in7(pull_resistor_1_node), .in8(pull_resistor_1_node),
    .in9(pull_resistor_1_node), .in10(pull_resistor_1_node), .in11(pull_resistor_1_node),
    .in12(pull_resistor_1_node), .in13(pull_resistor_1_node), .in14(pull_resistor_1_node),
    .in15(pull_resistor_1_node), .out(Y[3]), .sel(B[3:0]));
  Multiplexer #(.select(4)) multiplexer_14 (
    .in0(A[2]), .in1(A[1]), .in2(A[0]), .in3(pull_resistor_1_node), .in4(pull_resistor_1_node),
    .in5(pull_resistor_1_node), .in6(pull_resistor_1_node), .in7(pull_resistor_1_node),
    .in8(pull_resistor_1_node), .in9(pull_resistor_1_node), .in10(pull_resistor_1_node),
    .in11(pull_resistor_1_node), .in12(pull_resistor_1_node), .in13(pull_resistor_1_node),
    .in14(pull_resistor_1_node), .in15(pull_resistor_1_node), .out(Y[2]), .sel(B[3:0]));
  Multiplexer #(.select(4)) multiplexer_15 (
    .in0(A[1]), .in1(A[0]), .in2(pull_resistor_1_node), .in3(pull_resistor_1_node),
    .in4(pull_resistor_1_node), .in5(pull_resistor_1_node), .in6(pull_resistor_1_node),
    .in7(pull_resistor_1_node), .in8(pull_resistor_1_node), .in9(pull_resistor_1_node),
    .in10(pull_resistor_1_node), .in11(pull_resistor_1_node), .in12(pull_resistor_1_node),
    .in13(pull_resistor_1_node), .in14(pull_resistor_1_node), .in15(pull_resistor_1_node), .out(Y[1]),
    .sel(B[3:0]));
  Multiplexer #(.select(4)) multiplexer_16 (
    .in0(A[0]), .in1(pull_resistor_1_node), .in2(pull_resistor_1_node), .in3(pull_resistor_1_node),
    .in4(pull_resistor_1_node), .in5(pull_resistor_1_node), .in6(pull_resistor_1_node),
    .in7(pull_resistor_1_node), .in8(pull_resistor_1_node), .in9(pull_resistor_1_node),
    .in10(pull_resistor_1_node), .in11(pull_resistor_1_node), .in12(pull_resistor_1_node),
    .in13(pull_resistor_1_node), .in14(pull_resistor_1_node), .in15(pull_resistor_1_node), .out(Y[0]),
    .sel(B[3:0]));
  Pull_Resistor pull_resistor_1 (.node(pull_resistor_1_node));
endmodule

module logicshifter (
  input  [15:0] B,
  input  Right,
  input  [15:0] A,
  output [15:0] rY,
  output [15:0] Y
);

  wire pull_resistor_1_node;
  wire [15:0] multiplexer_1_out;

  Multiplexer multiplexer_1 (.in0(A[0]), .in1(A[15]), .out(multiplexer_1_out[0]), .sel(Right));
  Multiplexer multiplexer_2 (.in0(A[1]), .in1(A[14]), .out(multiplexer_1_out[1]), .sel(Right));
  Multiplexer multiplexer_3 (.in0(A[2]), .in1(A[13]), .out(multiplexer_1_out[2]), .sel(Right));
  Multiplexer multiplexer_4 (.in0(A[3]), .in1(A[12]), .out(multiplexer_1_out[3]), .sel(Right));
  Multiplexer multiplexer_5 (.in0(A[4]), .in1(A[11]), .out(multiplexer_1_out[4]), .sel(Right));
  Multiplexer multiplexer_6 (.in0(A[5]), .in1(A[10]), .out(multiplexer_1_out[5]), .sel(Right));
  Multiplexer multiplexer_7 (.in0(A[6]), .in1(A[9]), .out(multiplexer_1_out[6]), .sel(Right));
  Multiplexer multiplexer_8 (.in0(A[7]), .in1(A[8]), .out(multiplexer_1_out[7]), .sel(Right));
  Multiplexer multiplexer_9 (.in0(A[8]), .in1(A[7]), .out(multiplexer_1_out[8]), .sel(Right));
  Multiplexer multiplexer_10 (.in0(A[9]), .in1(A[6]), .out(multiplexer_1_out[9]), .sel(Right));
  Multiplexer multiplexer_11 (.in0(A[10]), .in1(A[5]), .out(multiplexer_1_out[10]), .sel(Right));
  Multiplexer multiplexer_12 (.in0(A[11]), .in1(A[4]), .out(multiplexer_1_out[11]), .sel(Right));
  Multiplexer multiplexer_13 (.in0(A[12]), .in1(A[3]), .out(multiplexer_1_out[12]), .sel(Right));
  Multiplexer multiplexer_14 (.in0(A[13]), .in1(A[2]), .out(multiplexer_1_out[13]), .sel(Right));
  Multiplexer multiplexer_15 (.in0(A[14]), .in1(A[1]), .out(multiplexer_1_out[14]), .sel(Right));
  Multiplexer multiplexer_16 (.in0(A[15]), .in1(A[0]), .out(multiplexer_1_out[15]), .sel(Right));
  Multiplexer #(.select(4)) multiplexer_17 (
    .in0(multiplexer_1_out[15]), .in1(multiplexer_1_out[14]), .in2(multiplexer_1_out[13]),
    .in3(multiplexer_1_out[12]), .in4(multiplexer_1_out[11]), .in5(multiplexer_1_out[10]),
    .in6(multiplexer_1_out[9]), .in7(multiplexer_1_out[8]), .in8(multiplexer_1_out[7]),
    .in9(multiplexer_1_out[6]), .in10(multiplexer_1_out[5]), .in11(multiplexer_1_out[4]),
    .in12(multiplexer_1_out[3]), .in13(multiplexer_1_out[2]), .in14(multiplexer_1_out[1]),
    .in15(multiplexer_1_out[0]), .out(rY[0]), .sel(B[3:0]));
  Multiplexer #(.select(4)) multiplexer_18 (
    .in0(multiplexer_1_out[14]), .in1(multiplexer_1_out[13]), .in2(multiplexer_1_out[12]),
    .in3(multiplexer_1_out[11]), .in4(multiplexer_1_out[10]), .in5(multiplexer_1_out[9]),
    .in6(multiplexer_1_out[8]), .in7(multiplexer_1_out[7]), .in8(multiplexer_1_out[6]),
    .in9(multiplexer_1_out[5]), .in10(multiplexer_1_out[4]), .in11(multiplexer_1_out[3]),
    .in12(multiplexer_1_out[2]), .in13(multiplexer_1_out[1]), .in14(multiplexer_1_out[0]),
    .in15(pull_resistor_1_node), .out(rY[1]), .sel(B[3:0]));
  Multiplexer #(.select(4)) multiplexer_19 (
    .in0(multiplexer_1_out[13]), .in1(multiplexer_1_out[12]), .in2(multiplexer_1_out[11]),
    .in3(multiplexer_1_out[10]), .in4(multiplexer_1_out[9]), .in5(multiplexer_1_out[8]),
    .in6(multiplexer_1_out[7]), .in7(multiplexer_1_out[6]), .in8(multiplexer_1_out[5]),
    .in9(multiplexer_1_out[4]), .in10(multiplexer_1_out[3]), .in11(multiplexer_1_out[2]),
    .in12(multiplexer_1_out[1]), .in13(multiplexer_1_out[0]), .in14(pull_resistor_1_node),
    .in15(pull_resistor_1_node), .out(rY[2]), .sel(B[3:0]));
  Multiplexer #(.select(4)) multiplexer_20 (
    .in0(multiplexer_1_out[12]), .in1(multiplexer_1_out[11]), .in2(multiplexer_1_out[10]),
    .in3(multiplexer_1_out[9]), .in4(multiplexer_1_out[8]), .in5(multiplexer_1_out[7]),
    .in6(multiplexer_1_out[6]), .in7(multiplexer_1_out[5]), .in8(multiplexer_1_out[4]),
    .in9(multiplexer_1_out[3]), .in10(multiplexer_1_out[2]), .in11(multiplexer_1_out[1]),
    .in12(multiplexer_1_out[0]), .in13(pull_resistor_1_node), .in14(pull_resistor_1_node),
    .in15(pull_resistor_1_node), .out(rY[3]), .sel(B[3:0]));
  Multiplexer #(.select(4)) multiplexer_21 (
    .in0(multiplexer_1_out[11]), .in1(multiplexer_1_out[10]), .in2(multiplexer_1_out[9]),
    .in3(multiplexer_1_out[8]), .in4(multiplexer_1_out[7]), .in5(multiplexer_1_out[6]),
    .in6(multiplexer_1_out[5]), .in7(multiplexer_1_out[4]), .in8(multiplexer_1_out[3]),
    .in9(multiplexer_1_out[2]), .in10(multiplexer_1_out[1]), .in11(multiplexer_1_out[0]),
    .in12(pull_resistor_1_node), .in13(pull_resistor_1_node), .in14(pull_resistor_1_node),
    .in15(pull_resistor_1_node), .out(rY[4]), .sel(B[3:0]));
  Multiplexer #(.select(4)) multiplexer_22 (
    .in0(multiplexer_1_out[10]), .in1(multiplexer_1_out[9]), .in2(multiplexer_1_out[8]),
    .in3(multiplexer_1_out[7]), .in4(multiplexer_1_out[6]), .in5(multiplexer_1_out[5]),
    .in6(multiplexer_1_out[4]), .in7(multiplexer_1_out[3]), .in8(multiplexer_1_out[2]),
    .in9(multiplexer_1_out[1]), .in10(multiplexer_1_out[0]), .in11(pull_resistor_1_node),
    .in12(pull_resistor_1_node), .in13(pull_resistor_1_node), .in14(pull_resistor_1_node),
    .in15(pull_resistor_1_node), .out(rY[5]), .sel(B[3:0]));
  Multiplexer #(.select(4)) multiplexer_23 (
    .in0(multiplexer_1_out[9]), .in1(multiplexer_1_out[8]), .in2(multiplexer_1_out[7]),
    .in3(multiplexer_1_out[6]), .in4(multiplexer_1_out[5]), .in5(multiplexer_1_out[4]),
    .in6(multiplexer_1_out[3]), .in7(multiplexer_1_out[2]), .in8(multiplexer_1_out[1]),
    .in9(multiplexer_1_out[0]), .in10(pull_resistor_1_node), .in11(pull_resistor_1_node),
    .in12(pull_resistor_1_node), .in13(pull_resistor_1_node), .in14(pull_resistor_1_node),
    .in15(pull_resistor_1_node), .out(rY[6]), .sel(B[3:0]));
  Multiplexer #(.select(4)) multiplexer_24 (
    .in0(multiplexer_1_out[8]), .in1(multiplexer_1_out[7]), .in2(multiplexer_1_out[6]),
    .in3(multiplexer_1_out[5]), .in4(multiplexer_1_out[4]), .in5(multiplexer_1_out[3]),
    .in6(multiplexer_1_out[2]), .in7(multiplexer_1_out[1]), .in8(multiplexer_1_out[0]),
    .in9(pull_resistor_1_node), .in10(pull_resistor_1_node), .in11(pull_resistor_1_node),
    .in12(pull_resistor_1_node), .in13(pull_resistor_1_node), .in14(pull_resistor_1_node),
    .in15(pull_resistor_1_node), .out(rY[7]), .sel(B[3:0]));
  Multiplexer #(.select(4)) multiplexer_25 (
    .in0(multiplexer_1_out[7]), .in1(multiplexer_1_out[6]), .in2(multiplexer_1_out[5]),
    .in3(multiplexer_1_out[4]), .in4(multiplexer_1_out[3]), .in5(multiplexer_1_out[2]),
    .in6(multiplexer_1_out[1]), .in7(multiplexer_1_out[0]), .in8(pull_resistor_1_node),
    .in9(pull_resistor_1_node), .in10(pull_resistor_1_node), .in11(pull_resistor_1_node),
    .in12(pull_resistor_1_node), .in13(pull_resistor_1_node), .in14(pull_resistor_1_node),
    .in15(pull_resistor_1_node), .out(rY[8]), .sel(B[3:0]));
  Multiplexer #(.select(4)) multiplexer_26 (
    .in0(multiplexer_1_out[6]), .in1(multiplexer_1_out[5]), .in2(multiplexer_1_out[4]),
    .in3(multiplexer_1_out[3]), .in4(multiplexer_1_out[2]), .in5(multiplexer_1_out[1]),
    .in6(multiplexer_1_out[0]), .in7(pull_resistor_1_node), .in8(pull_resistor_1_node),
    .in9(pull_resistor_1_node), .in10(pull_resistor_1_node), .in11(pull_resistor_1_node),
    .in12(pull_resistor_1_node), .in13(pull_resistor_1_node), .in14(pull_resistor_1_node),
    .in15(pull_resistor_1_node), .out(rY[9]), .sel(B[3:0]));
  Multiplexer #(.select(4)) multiplexer_27 (
    .in0(multiplexer_1_out[5]), .in1(multiplexer_1_out[4]), .in2(multiplexer_1_out[3]),
    .in3(multiplexer_1_out[2]), .in4(multiplexer_1_out[1]), .in5(multiplexer_1_out[0]),
    .in6(pull_resistor_1_node), .in7(pull_resistor_1_node), .in8(pull_resistor_1_node),
    .in9(pull_resistor_1_node), .in10(pull_resistor_1_node), .in11(pull_resistor_1_node),
    .in12(pull_resistor_1_node), .in13(pull_resistor_1_node), .in14(pull_resistor_1_node),
    .in15(pull_resistor_1_node), .out(rY[10]), .sel(B[3:0]));
  Multiplexer #(.select(4)) multiplexer_28 (
    .in0(multiplexer_1_out[4]), .in1(multiplexer_1_out[3]), .in2(multiplexer_1_out[2]),
    .in3(multiplexer_1_out[1]), .in4(multiplexer_1_out[0]), .in5(pull_resistor_1_node),
    .in6(pull_resistor_1_node), .in7(pull_resistor_1_node), .in8(pull_resistor_1_node),
    .in9(pull_resistor_1_node), .in10(pull_resistor_1_node), .in11(pull_resistor_1_node),
    .in12(pull_resistor_1_node), .in13(pull_resistor_1_node), .in14(pull_resistor_1_node),
    .in15(pull_resistor_1_node), .out(rY[11]), .sel(B[3:0]));
  Multiplexer #(.select(4)) multiplexer_29 (
    .in0(multiplexer_1_out[3]), .in1(multiplexer_1_out[2]), .in2(multiplexer_1_out[1]),
    .in3(multiplexer_1_out[0]), .in4(pull_resistor_1_node), .in5(pull_resistor_1_node),
    .in6(pull_resistor_1_node), .in7(pull_resistor_1_node), .in8(pull_resistor_1_node),
    .in9(pull_resistor_1_node), .in10(pull_resistor_1_node), .in11(pull_resistor_1_node),
    .in12(pull_resistor_1_node), .in13(pull_resistor_1_node), .in14(pull_resistor_1_node),
    .in15(pull_resistor_1_node), .out(rY[12]), .sel(B[3:0]));
  Multiplexer #(.select(4)) multiplexer_30 (
    .in0(multiplexer_1_out[2]), .in1(multiplexer_1_out[1]), .in2(multiplexer_1_out[0]),
    .in3(pull_resistor_1_node), .in4(pull_resistor_1_node), .in5(pull_resistor_1_node),
    .in6(pull_resistor_1_node), .in7(pull_resistor_1_node), .in8(pull_resistor_1_node),
    .in9(pull_resistor_1_node), .in10(pull_resistor_1_node), .in11(pull_resistor_1_node),
    .in12(pull_resistor_1_node), .in13(pull_resistor_1_node), .in14(pull_resistor_1_node),
    .in15(pull_resistor_1_node), .out(rY[13]), .sel(B[3:0]));
  Multiplexer #(.select(4)) multiplexer_31 (
    .in0(multiplexer_1_out[1]), .in1(multiplexer_1_out[0]), .in2(pull_resistor_1_node),
    .in3(pull_resistor_1_node), .in4(pull_resistor_1_node), .in5(pull_resistor_1_node),
    .in6(pull_resistor_1_node), .in7(pull_resistor_1_node), .in8(pull_resistor_1_node),
    .in9(pull_resistor_1_node), .in10(pull_resistor_1_node), .in11(pull_resistor_1_node),
    .in12(pull_resistor_1_node), .in13(pull_resistor_1_node), .in14(pull_resistor_1_node),
    .in15(pull_resistor_1_node), .out(rY[14]), .sel(B[3:0]));
  Multiplexer #(.select(4)) multiplexer_32 (
    .in0(multiplexer_1_out[0]), .in1(pull_resistor_1_node), .in2(pull_resistor_1_node),
    .in3(pull_resistor_1_node), .in4(pull_resistor_1_node), .in5(pull_resistor_1_node),
    .in6(pull_resistor_1_node), .in7(pull_resistor_1_node), .in8(pull_resistor_1_node),
    .in9(pull_resistor_1_node), .in10(pull_resistor_1_node), .in11(pull_resistor_1_node),
    .in12(pull_resistor_1_node), .in13(pull_resistor_1_node), .in14(pull_resistor_1_node),
    .in15(pull_resistor_1_node), .out(rY[15]), .sel(B[3:0]));
  Pull_Resistor pull_resistor_1 (.node(pull_resistor_1_node));

  assign Y = {rY[0], rY[1], rY[2], rY[3], rY[4], rY[5], rY[6], rY[7], rY[8], rY[9], rY[10], rY[11], rY[12], rY[13], rY[14], rY[15]};
endmodule

module aluMICROCODED (
  input  [3:0] OP,
  input  CLK,
  input  [15:0] Din,
  output FS,
  output FO,
  output FC,
  output FZ,
  output [15:0] Dout
);

  wire and_1_out, and_2_out, not_1_out, pull_resistor_1_node;
  wire [15:0] alu_1_y, register_1_q, register_2_q;

  and and_1 (and_1_out, ~OP[0], OP[3]);  // AND_Gate
  and and_2 (and_2_out, OP[0], OP[3]);
  not not_1 (not_1_out, OP[3]);
  assign Dout = not_1_out ? alu_1_y : 16'bz;  // Controlled_Buffer controlled_buffer_1
  Register #(.width(16)) register_1 (.D(Din), .en(and_1_out), .clk(CLK), .Q(register_1_q), .clr(pull_resistor_1_node));
  Register #(.width(16)) register_2 (.D(Din), .en(and_2_out), .clk(CLK), .Q(register_2_q), .clr(pull_resistor_1_node));
  Pull_Resistor pull_resistor_1 (.node(pull_resistor_1_node));
  alu alu_1 (.funct(OP[2:0]), .A(register_1_q), .B(register_2_q), .Y(alu_1_y), .FZ(FZ), .FO(FO), .FC(FC), .FS(FS));
endmodule
