// Logisim project ALU.circ as structural Verilog: 11 circuits, main circuit add
module add (
  input  [15:0] B,
  input  [15:0] A,
  output [15:0] Y,
  output Cout,
  output MsbCin
);

  wire n74283_1_pin9, n74283_2_pin9, n74283_3_pin9;

  fulladd4b fulladd4b_1 (
    .B0(B[12]), .B1(B[13]), .B2(B[14]), .B3(B[15]), .A0(A[12]), .A1(A[13]), .A2(A[14]), .A3(A[15]),
    .Cin(n74283_3_pin9), .MsbCin(MsbCin), .Cout(Cout), .Y0(Y[12]), .Y1(Y[13]), .Y2(Y[14]), .Y3(Y[15]));
  _74283 u_74283_1 (
    .pin1(Y[1]), .pin2(B[1]), .pin3(A[1]), .pin4(Y[0]), .pin5(A[0]), .pin6(B[0]), .pin15(B[2]), .pin14(A[2]),
    .pin13(Y[2]), .pin12(A[3]), .pin11(B[3]), .pin10(Y[3]), .pin9(n74283_1_pin9));  // open: pin7
  _74283 u_74283_2 (
    .pin1(Y[5]), .pin2(B[5]), .pin3(A[5]), .pin4(Y[4]), .pin5(A[4]), .pin6(B[4]), .pin7(n74283_1_pin9),
    .pin15(B[6]), .pin14(A[6]), .pin13(Y[6]), .pin12(A[7]), .pin11(B[7]), .pin10(Y[7]), .pin9(n74283_2_pin9));
  _74283 u_74283_3 (
    .pin1(Y[9]), .pin2(B[9]), .pin3(A[9]), .pin4(Y[8]), .pin5(A[8]), .pin6(B[8]), .pin7(n74283_2_pin9),
    .pin15(B[10]), .pin14(A[10]), .pin13(Y[10]), .pin12(A[11]), .pin11(B[11]), .pin10(Y[11]),
    .pin9(n74283_3_pin9));
endmodule

module sub (
  input  [15:0] A,
  input  [15:0] B,
  output Cout,
  output MsbCin,
  output [15:0] Y
);

  wire n74283_1_pin7, n74283_1_pin9, n74283_2_pin9, n74283_3_pin9;
  wire [15:0] n7404_1_pin2;

  _7404 u_7404_1 (
    .pin1(B[0]), .pin2(n7404_1_pin2[0]), .pin3(B[1]), .pin4(n7404_1_pin2[1]), .pin5(B[2]),
    .pin6(n7404_1_pin2[2]), .pin13(B[8]), .pin12(n7404_1_pin2[8]), .pin11(B[9]), .pin10(n7404_1_pin2[9]),
    .pin9(B[10]), .pin8(n7404_1_pin2[10]));
  _7404 u_7404_2 (
    .pin1(B[3]), .pin2(n7404_1_pin2[3]), .pin3(B[4]), .pin4(n7404_1_pin2[4]), .pin5(B[5]),
    .pin6(n7404_1_pin2[5]), .pin13(B[11]), .pin12(n7404_1_pin2[11]), .pin11(B[12]), .pin10(n7404_1_pin2[12]),
    .pin9(B[13]), .pin8(n7404_1_pin2[13]));
  _7404 u_7404_3 (
    .pin1(B[6]), .pin2(n7404_1_pin2[6]), .pin3(B[7]), .pin4(n7404_1_pin2[7]), .pin13(B[14]),
    .pin12(n7404_1_pin2[14]), .pin11(B[15]), .pin10(n7404_1_pin2[15]));  // open: pin5, pin6, pin9, pin8
  fulladd4b fulladd4b_1 (
    .B0(A[12]), .B1(A[13]), .B2(A[14]), .B3(A[15]), .A0(n7404_1_pin2[12]), .A1(n7404_1_pin2[13]),
    .A2(n7404_1_pin2[14]), .A3(n7404_1_pin2[15]), .Cin(n74283_3_pin9), .MsbCin(MsbCin), .Cout(Cout),
    .Y0(Y[12]), .Y1(Y[13]), .Y2(Y[14]), .Y3(Y[15]));
  _74283 u_74283_1 (
    .pin1(Y[1]), .pin2(n7404_1_pin2[1]), .pin3(A[1]), .pin4(Y[0]), .pin5(A[0]), .pin6(n7404_1_pin2[0]),
    .pin7(n74283_1_pin7), .pin15(n7404_1_pin2[2]), .pin14(A[2]), .pin13(Y[2]), .pin12(A[3]),
    .pin11(n7404_1_pin2[3]), .pin10(Y[3]), .pin9(n74283_1_pin9));
  _74283 u_74283_2 (
    .pin1(Y[5]), .pin2(n7404_1_pin2[5]), .pin3(A[5]), .pin4(Y[4]), .pin5(A[4]), .pin6(n7404_1_pin2[4]),
    .pin7(n74283_1_pin9), .pin15(n7404_1_pin2[6]), .pin14(A[6]), .pin13(Y[6]), .pin12(A[7]),
    .pin11(n7404_1_pin2[7]), .pin10(Y[7]), .pin9(n74283_2_pin9));
  _74283 u_74283_3 (
    .pin1(Y[9]), .pin2(n7404_1_pin2[9]), .pin3(A[9]), .pin4(Y[8]), .pin5(A[8]), .pin6(n7404_1_pin2[8]),
    .pin7(n74283_2_pin9), .pin15(n7404_1_pin2[10]), .pin14(A[10]), .pin13(Y[10]), .pin12(A[11]),
    .pin11(n7404_1_pin2[11]), .pin10(Y[11]), .pin9(n74283_3_pin9));
  // also tied to VCC on the sheet: n74283_1_pin7
endmodule

module alu (
  input  [15:0] A,
  input  [15:0] B,
  input  [2:0] funct,
  output FO,
  output FC,
  output FS,
  output [15:0] Y,
  output FZ
);

  wire add_1_cout, add_1_msbcin, multiplexer_1_out, multiplexer_2_out, nor_1_out, sub_1_cout, sub_1_msbcin,
       xor_1_out;
  wire [3:0] add_1_y, add_1_y_2, add_1_y_3, add_1_y_4, and16b_1_y, and16b_1_y_2, and16b_1_y_3, and16b_1_y_4,
       logicshifter_1_y, logicshifter_1_y_2, logicshifter_1_y_3, logicshifter_1_y_4, not16b_1_y,
       not16b_1_y_2, not16b_1_y_3, not16b_1_y_4, or16b_1_y, or16b_1_y_2, or16b_1_y_3, or16b_1_y_4, sub_1_y,
       sub_1_y_2, sub_1_y_3, sub_1_y_4, xor16b_1_y, xor16b_1_y_2, xor16b_1_y_3, xor16b_1_y_4;
  wire [15:0] logicshifter_1_ry, multiplexer_3_out;

  Hex_Digit_Display #(.decimalPoint("false")) hex_digit_display_1 (.value(add_1_y_4));
  Hex_Digit_Display #(.decimalPoint("false")) hex_digit_display_2 (.value(add_1_y_3));
  Hex_Digit_Display #(.decimalPoint("false")) hex_digit_display_3 (.value(add_1_y_2));
  add add_1 (.A(A), .B(B), .Cout(add_1_cout), .MsbCin(add_1_msbcin), .Y({add_1_y_4, add_1_y_3, add_1_y_2, add_1_y}));
  Hex_Digit_Display #(.decimalPoint("false")) hex_digit_display_4 (.value(add_1_y));
  Multiplexer multiplexer_1 (.in0(add_1_cout), .in1(sub_1_msbcin), .out(multiplexer_1_out), .sel(funct[0]));
  xor xor_1 (xor_1_out, multiplexer_1_out, multiplexer_2_out);
  buf buffer_1 (FO, xor_1_out);
  Hex_Digit_Display #(.decimalPoint("false")) hex_digit_display_5 (.value(sub_1_y_4));
  Multiplexer multiplexer_2 (.in0(add_1_msbcin), .in1(sub_1_cout), .out(multiplexer_2_out), .sel(funct[0]));
  buf buffer_2 (FC, multiplexer_2_out);
  Hex_Digit_Display #(.decimalPoint("false")) hex_digit_display_6 (.value(sub_1_y_2));
  Hex_Digit_Display #(.decimalPoint("false")) hex_digit_display_7 (.value(sub_1_y_3));
  sub sub_1 (.A(A), .B(B), .Y({sub_1_y_4, sub_1_y_3, sub_1_y_2, sub_1_y}), .Cout(sub_1_cout), .MsbCin(sub_1_msbcin));
  buf buffer_3 (FS, multiplexer_3_out[15]);
  Hex_Digit_Display #(.decimalPoint("false")) hex_digit_display_8 (.value(sub_1_y));
  Multiplexer #(.select(3), .width(16)) multiplexer_3 (
    .in0({add_1_y_4, add_1_y_3, add_1_y_2, add_1_y}), .in1({sub_1_y_4, sub_1_y_3, sub_1_y_2, sub_1_y}),
    .in2({and16b_1_y_4, and16b_1_y_3, and16b_1_y_2, and16b_1_y}),
    .in3({or16b_1_y_4, or16b_1_y_3, or16b_1_y_2, or16b_1_y}),
    .in4({xor16b_1_y_4, xor16b_1_y_3, xor16b_1_y_2, xor16b_1_y}),
    .in5({not16b_1_y_4, not16b_1_y_3, not16b_1_y_2, not16b_1_y}),
    .in6({logicshifter_1_y_4, logicshifter_1_y_3, logicshifter_1_y_2, logicshifter_1_y}),
    .in7(logicshifter_1_ry), .out(multiplexer_3_out), .sel(funct));
  assign Y = multiplexer_3_out;  // Buffer buffer_4, 16 bits wide
  Hex_Digit_Display #(.decimalPoint("false")) hex_digit_display_9 (.value(and16b_1_y_4));
  Hex_Digit_Display #(.decimalPoint("false")) hex_digit_display_10 (.value(and16b_1_y_3));
  and16b and16b_1 (.B(B), .A(A), .Y({and16b_1_y_4, and16b_1_y_3, and16b_1_y_2, and16b_1_y}));
  Hex_Digit_Display #(.decimalPoint("false")) hex_digit_display_11 (.value(and16b_1_y_2));
  Hex_Digit_Display #(.decimalPoint("false")) hex_digit_display_12 (.value(and16b_1_y));
  nor nor_1 (nor_1_out, multiplexer_3_out[15], multiplexer_3_out[14], multiplexer_3_out[13], multiplexer_3_out[12], multiplexer_3_out[11], multiplexer_3_out[10], multiplexer_3_out[9], multiplexer_3_out[8], multiplexer_3_out[6], multiplexer_3_out[5], multiplexer_3_out[4], multiplexer_3_out[3], multiplexer_3_out[2], multiplexer_3_out[1], multiplexer_3_out[0], multiplexer_3_out[7]);
  buf buffer_5 (FZ, nor_1_out);
  Hex_Digit_Display #(.decimalPoint("false")) hex_digit_display_13 (.value(or16b_1_y_4));
  Hex_Digit_Display #(.decimalPoint("false")) hex_digit_display_14 (.value(or16b_1_y_3));
  Hex_Digit_Display #(.decimalPoint("false")) hex_digit_display_15 (.value(or16b_1_y_2));
  or16b or16b_1 (.B(B), .A(A), .Y({or16b_1_y_4, or16b_1_y_3, or16b_1_y_2, or16b_1_y}));
  Hex_Digit_Display #(.decimalPoint("false")) hex_digit_display_16 (.value(or16b_1_y));
  Hex_Digit_Display #(.decimalPoint("false")) hex_digit_display_17 (.value(xor16b_1_y_4));
  Hex_Digit_Display #(.decimalPoint("false")) hex_digit_display_18 (.value(xor16b_1_y_3));
  xor16b xor16b_1 (.A(A), .B(B), .Y({xor16b_1_y_4, xor16b_1_y_3, xor16b_1_y_2, xor16b_1_y}));
  Hex_Digit_Display #(.decimalPoint("false")) hex_digit_display_19 (.value(xor16b_1_y_2));
  Hex_Digit_Display #(.decimalPoint("false")) hex_digit_display_20 (.value(xor16b_1_y));
  Hex_Digit_Display #(.decimalPoint("false")) hex_digit_display_21 (.value(not16b_1_y_4));
  Hex_Digit_Display #(.decimalPoint("false")) hex_digit_display_22 (.value(not16b_1_y_3));
  not16b not16b_1 (.B(B), .Y({not16b_1_y_4, not16b_1_y_3, not16b_1_y_2, not16b_1_y}));
  Hex_Digit_Display #(.decimalPoint("false")) hex_digit_display_23 (.value(not16b_1_y_2));
  Hex_Digit_Display #(.decimalPoint("false")) hex_digit_display_24 (.value(not16b_1_y));
  Hex_Digit_Display #(.decimalPoint("false")) hex_digit_display_25 (.value(logicshifter_1_y_4));
  Hex_Digit_Display #(.decimalPoint("false")) hex_digit_display_26 (.value(logicshifter_1_y_3));
  Hex_Digit_Display #(.decimalPoint("false")) hex_digit_display_27 (.value(logicshifter_1_y_2));
  logicshifter logicshifter_1 (
    .B(B), .A(A), .Right(funct[0]),
    .Y({logicshifter_1_y_4, logicshifter_1_y_3, logicshifter_1_y_2, logicshifter_1_y}), .rY(logicshifter_1_ry));
  Hex_Digit_Display #(.decimalPoint("false")) hex_digit_display_28 (.value(logicshifter_1_y));
endmodule

module fulladd4b (
  input  Cin,
  input  A0,
  input  B0,
  input  A1,
  input  B1,
  input  A2,
  input  B2,
  input  A3,
  input  B3,
  output Y0,
  output Y1,
  output Y2,
  output MsbCin,
  output Cout,
  output Y3
);

  wire n7408_1_pin3, n7408_1_pin6, n7408_1_pin8, n7408_1_pin11, n7408_2_pin3, n7408_2_pin6, n7408_2_pin8,
       n7408_2_pin11, n7486_1_pin3, n7486_1_pin5, n7486_1_pin11, n7486_2_pin3, n7486_2_pin9, n7486_2_pin11;

  _7486 u_7486_1 (
    .pin1(A1), .pin2(B1), .pin3(n7486_1_pin3), .pin4(n7486_1_pin3), .pin5(n7486_1_pin5), .pin6(Y1),
    .pin13(B0), .pin12(A0), .pin11(n7486_1_pin11), .pin10(n7486_1_pin11), .pin9(Cin), .pin8(Y0));
  _7486 u_7486_2 (
    .pin1(A3), .pin2(B3), .pin3(n7486_2_pin3), .pin4(n7486_2_pin3), .pin5(MsbCin), .pin6(Y3), .pin13(B2),
    .pin12(A2), .pin11(n7486_2_pin11), .pin10(n7486_2_pin11), .pin9(n7486_2_pin9), .pin8(Y2));
  _7408 u_7408_1 (
    .pin1(B1), .pin2(A1), .pin3(n7408_1_pin3), .pin4(n7486_1_pin3), .pin5(n7486_1_pin5), .pin6(n7408_1_pin6),
    .pin13(A0), .pin12(B0), .pin11(n7408_1_pin11), .pin10(n7486_1_pin11), .pin9(Cin), .pin8(n7408_1_pin8));
  _7408 u_7408_2 (
    .pin1(B3), .pin2(A3), .pin3(n7408_2_pin3), .pin4(n7486_2_pin3), .pin5(MsbCin), .pin6(n7408_2_pin6),
    .pin13(A2), .pin12(B2), .pin11(n7408_2_pin11), .pin10(n7486_2_pin11), .pin9(n7486_2_pin9),
    .pin8(n7408_2_pin8));
  _7432 u_7432_1 (
    .pin1(n7408_2_pin11), .pin2(n7408_2_pin8), .pin3(MsbCin), .pin4(n7408_2_pin6), .pin5(n7408_2_pin3),
    .pin6(Cout), .pin13(n7408_1_pin8), .pin12(n7408_1_pin11), .pin11(n7486_1_pin5), .pin10(n7408_1_pin6),
    .pin9(n7408_1_pin3), .pin8(n7486_2_pin9));
endmodule

module and16b (
  input  [15:0] A,
  input  [15:0] B,
  output [15:0] Y
);

  _7408 u_7408_1 (
    .pin1(A[2]), .pin2(B[2]), .pin3(Y[2]), .pin4(A[3]), .pin5(B[3]), .pin6(Y[3]), .pin13(A[1]), .pin12(B[1]),
    .pin11(Y[1]), .pin10(A[0]), .pin9(B[0]), .pin8(Y[0]));
  _7408 u_7408_2 (
    .pin1(A[6]), .pin2(B[6]), .pin3(Y[6]), .pin4(A[7]), .pin5(B[7]), .pin6(Y[7]), .pin13(A[5]), .pin12(B[5]),
    .pin11(Y[5]), .pin10(A[4]), .pin9(B[4]), .pin8(Y[4]));
  _7408 u_7408_3 (
    .pin1(A[10]), .pin2(B[10]), .pin3(Y[10]), .pin4(A[11]), .pin5(B[11]), .pin6(Y[11]), .pin13(A[9]),
    .pin12(B[9]), .pin11(Y[9]), .pin10(A[8]), .pin9(B[8]), .pin8(Y[8]));
  _7408 u_7408_4 (
    .pin1(A[14]), .pin2(B[14]), .pin3(Y[14]), .pin4(A[15]), .pin5(B[15]), .pin6(Y[15]), .pin13(A[13]),
    .pin12(B[13]), .pin11(Y[13]), .pin10(A[12]), .pin9(B[12]), .pin8(Y[12]));
endmodule

module or16b (
  input  [15:0] A,
  input  [15:0] B,
  output [15:0] Y
);

  _7432 u_7432_1 (
    .pin1(A[2]), .pin2(B[2]), .pin3(Y[2]), .pin4(A[3]), .pin5(B[3]), .pin6(Y[3]), .pin13(A[1]), .pin12(B[1]),
    .pin11(Y[1]), .pin10(A[0]), .pin9(B[0]), .pin8(Y[0]));
  _7432 u_7432_2 (
    .pin1(A[6]), .pin2(B[6]), .pin3(Y[6]), .pin4(A[7]), .pin5(B[7]), .pin6(Y[7]), .pin13(A[5]), .pin12(B[5]),
    .pin11(Y[5]), .pin10(A[4]), .pin9(B[4]), .pin8(Y[4]));
  _7432 u_7432_3 (
    .pin1(A[10]), .pin2(B[10]), .pin3(Y[10]), .pin4(A[11]), .pin5(B[11]), .pin6(Y[11]), .pin13(A[9]),
    .pin12(B[9]), .pin11(Y[9]), .pin10(A[8]), .pin9(B[8]), .pin8(Y[8]));
  _7432 u_7432_4 (
    .pin1(A[14]), .pin2(B[14]), .pin3(Y[14]), .pin4(A[15]), .pin5(B[15]), .pin6(Y[15]), .pin13(A[13]),
    .pin12(B[13]), .pin11(Y[13]), .pin10(A[12]), .pin9(B[12]), .pin8(Y[12]));
endmodule

module xor16b (
  input  [15:0] A,
  input  [15:0] B,
  output [15:0] Y
);

  _7486 u_7486_1 (
    .pin1(A[2]), .pin2(B[2]), .pin3(Y[2]), .pin4(A[3]), .pin5(B[3]), .pin6(Y[3]), .pin13(A[1]), .pin12(B[1]),
    .pin11(Y[1]), .pin10(A[0]), .pin9(B[0]), .pin8(Y[0]));
  _7486 u_7486_2 (
    .pin1(A[6]), .pin2(B[6]), .pin3(Y[6]), .pin4(A[7]), .pin5(B[7]), .pin6(Y[7]), .pin13(A[5]), .pin12(B[5]),
    .pin11(Y[5]), .pin10(A[4]), .pin9(B[4]), .pin8(Y[4]));
  _7486 u_7486_3 (
    .pin1(A[10]), .pin2(B[10]), .pin3(Y[10]), .pin4(A[11]), .pin5(B[11]), .pin6(Y[11]), .pin13(A[9]),
    .pin12(B[9]), .pin11(Y[9]), .pin10(A[8]), .pin9(B[8]), .pin8(Y[8]));
  _7486 u_7486_4 (
    .pin1(A[14]), .pin2(B[14]), .pin3(Y[14]), .pin4(A[15]), .pin5(B[15]), .pin6(Y[15]), .pin13(A[13]),
    .pin12(B[13]), .pin11(Y[13]), .pin10(A[12]), .pin9(B[12]), .pin8(Y[12]));
endmodule

module not16b (
  input  [15:0] B,
  output [15:0] Y
);

  _7414 u_7414_1 (
    .pin1(B[3]), .pin2(Y[3]), .pin3(B[4]), .pin4(Y[4]), .pin5(B[5]), .pin6(Y[5]), .pin13(B[2]), .pin12(Y[2]),
    .pin11(B[1]), .pin10(Y[1]), .pin9(B[0]), .pin8(Y[0]));
  _7414 u_7414_2 (
    .pin1(B[9]), .pin2(Y[9]), .pin3(B[10]), .pin4(Y[10]), .pin5(B[11]), .pin6(Y[11]), .pin13(B[8]),
    .pin12(Y[8]), .pin11(B[7]), .pin10(Y[7]), .pin9(B[6]), .pin8(Y[6]));
  _7414 u_7414_3 (
    .pin1(B[15]), .pin2(Y[15]), .pin13(B[14]), .pin12(Y[14]), .pin11(B[13]), .pin10(Y[13]), .pin9(B[12]),
    .pin8(Y[12]));  // open: pin3, pin4, pin5, pin6
endmodule

module lsl (
  input  [15:0] B,
  input  [15:0] A,
  output [15:0] Y
);

  wire pull_resistor_1_node;

  Multiplexer #(.select(4)) multiplexer_1 (
    .in0(A[15]), .in1(A[14]), .in2(A[13]), .in3(A[12]), .in4(A[11]), .in5(A[10]), .in6(A[9]), .in7(A[8]),
    .in8(A[7]), .in9(A[6]), .in10(A[5]), .in11(A[4]), .in12(A[3]), .in13(A[2]), .in14(A[1]), .in15(A[0]),
    .out(Y[15]), .sel(B[3:0]));
  Multiplexer #(.select(4)) multiplexer_2 (
    .in0(A[14]), .in1(A[13]), .in2(A[12]), .in3(A[11]), .in4(A[10]), .in5(A[9]), .in6(A[8]), .in7(A[7]),
    .in8(A[6]), .in9(A[5]), .in10(A[4]), .in11(A[3]), .in12(A[2]), .in13(A[1]), .in14(A[0]),
    .in15(pull_resistor_1_node), .out(Y[14]), .sel(B[3:0]));
  Multiplexer #(.select(4)) multiplexer_3 (
    .in0(A[13]), .in1(A[12]), .in2(A[11]), .in3(A[10]), .in4(A[9]), .in5(A[8]), .in6(A[7]), .in7(A[6]),
    .in8(A[5]), .in9(A[4]), .in10(A[3]), .in11(A[2]), .in12(A[1]), .in13(A[0]), .in14(pull_resistor_1_node),
    .in15(pull_resistor_1_node), .out(Y[13]), .sel(B[3:0]));
  Multiplexer #(.select(4)) multiplexer_4 (
    .in0(A[12]), .in1(A[11]), .in2(A[10]), .in3(A[9]), .in4(A[8]), .in5(A[7]), .in6(A[6]), .in7(A[5]),
    .in8(A[4]), .in9(A[3]), .in10(A[2]), .in11(A[1]), .in12(A[0]), .in13(pull_resistor_1_node),
    .in14(pull_resistor_1_node), .in15(pull_resistor_1_node), .out(Y[12]), .sel(B[3:0]));
  Multiplexer #(.select(4)) multiplexer_5 (
    .in0(A[11]), .in1(A[10]), .in2(A[9]), .in3(A[8]), .in4(A[7]), .in5(A[6]), .in6(A[5]), .in7(A[4]),
    .in8(A[3]), .in9(A[2]), .in10(A[1]), .in11(A[0]), .in12(pull_resistor_1_node),
    .in13(pull_resistor_1_node), .in14(pull_resistor_1_node), .in15(pull_resistor_1_node), .out(Y[11]),
    .sel(B[3:0]));
  Multiplexer #(.select(4)) multiplexer_6 (
    .in0(A[10]), .in1(A[9]), .in2(A[8]), .in3(A[7]), .in4(A[6]), .in5(A[5]), .in6(A[4]), .in7(A[3]),
    .in8(A[2]), .in9(A[1]), .in10(A[0]), .in11(pull_resistor_1_node), .in12(pull_resistor_1_node),
    .in13(pull_resistor_1_node), .in14(pull_resistor_1_node), .in15(pull_resistor_1_node), .out(Y[10]),
    .sel(B[3:0]));
  Multiplexer #(.select(4)) multiplexer_7 (
    .in0(A[9]), .in1(A[8]), .in2(A[7]), .in3(A[6]), .in4(A[5]), .in5(A[4]), .in6(A[3]), .in7(A[2]),
    .in8(A[1]), .in9(A[0]), .in10(pull_resistor_1_node), .in11(pull_resistor_1_node),
    .in12(pull_resistor_1_node), .in13(pull_resistor_1_node), .in14(pull_resistor_1_node),
    .in15(pull_resistor_1_node), .out(Y[9]), .sel(B[3:0]));
  Multiplexer #(.select(4)) multiplexer_8 (
    .in0(A[8]), .in1(A[7]), .in2(A[6]), .in3(A[5]), .in4(A[4]), .in5(A[3]), .in6(A[2]), .in7(A[1]),
    .in8(A[0]), .in9(pull_resistor_1_node), .in10(pull_resistor_1_node), .in11(pull_resistor_1_node),
    .in12(pull_resistor_1_node), .in13(pull_resistor_1_node), .in14(pull_resistor_1_node),
    .in15(pull_resistor_1_node), .out(Y[8]), .sel(B[3:0]));
  Multiplexer #(.select(4)) multiplexer_9 (
    .in0(A[7]), .in1(A[6]), .in2(A[5]), .in3(A[4]), .in4(A[3]), .in5(A[2]), .in6(A[1]), .in7(A[0]),
    .in8(pull_resistor_1_node), .in9(pull_resistor_1_node), .in10(pull_resistor_1_node),
    .in11(pull_resistor_1_node), .in12(pull_resistor_1_node), .in13(pull_resistor_1_node),
    .in14(pull_resistor_1_node), .in15(pull_resistor_1_node), .out(Y[7]), .sel(B[3:0]));
  Multiplexer #(.select(4)) multiplexer_10 (
    .in0(A[6]), .in1(A[5]), .in2(A[4]), .in3(A[3]), .in4(A[2]), .in5(A[1]), .in6(A[0]),
    .in7(pull_resistor_1_node), .in8(pull_resistor_1_node), .in9(pull_resistor_1_node),
    .in10(pull_resistor_1_node), .in11(pull_resistor_1_node), .in12(pull_resistor_1_node),
    .in13(pull_resistor_1_node), .in14(pull_resistor_1_node), .in15(pull_resistor_1_node), .out(Y[6]),
    .sel(B[3:0]));
  Multiplexer #(.select(4)) multiplexer_11 (
    .in0(A[5]), .in1(A[4]), .in2(A[3]), .in3(A[2]), .in4(A[1]), .in5(A[0]), .in6(pull_resistor_1_node),
    .in7(pull_resistor_1_node), .in8(pull_resistor_1_node), .in9(pull_resistor_1_node),
    .in10(pull_resistor_1_node), .in11(pull_resistor_1_node), .in12(pull_resistor_1_node),
    .in13(pull_resistor_1_node), .in14(pull_resistor_1_node), .in15(pull_resistor_1_node), .out(Y[5]),
    .sel(B[3:0]));
  Multiplexer #(.select(4)) multiplexer_12 (
    .in0(A[4]), .in1(A[3]), .in2(A[2]), .in3(A[1]), .in4(A[0]), .in5(pull_resistor_1_node),
    .in6(pull_resistor_1_node), .in7(pull_resistor_1_node), .in8(pull_resistor_1_node),
    .in9(pull_resistor_1_node), .in10(pull_resistor_1_node), .in11(pull_resistor_1_node),
    .in12(pull_resistor_1_node), .in13(pull_resistor_1_node), .in14(pull_resistor_1_node),
    .in15(pull_resistor_1_node), .out(Y[4]), .sel(B[3:0]));
  Multiplexer #(.select(4)) multiplexer_13 (
    .in0(A[3]), .in1(A[2]), .in2(A[1]), .in3(A[0]), .in4(pull_resistor_1_node), .in5(pull_resistor_1_node),
    .in6(pull_resistor_1_node), .in7(pull_resistor_1_node), .in8(pull_resistor_1_node),
    .in9(pull_resistor_1_node), .in10(pull_resistor_1_node), .in11(pull_resistor_1_node),
    .in12(pull_resistor_1_node), .in13(pull_resistor_1_node), .in14(pull_resistor_1_node),
    .in15(pull_resistor_1_node), .out(Y[3]), .sel(B[3:0]));
  Multiplexer #(.select(4)) multiplexer_14 (
    .in0(A[2]), .in1(A[1]), .in2(A[0]), .in3(pull_resistor_1_node), .in4(pull_resistor_1_node),
    .in5(pull_resistor_1_node), .in6(pull_resistor_1_node), .in7(pull_resistor_1_node),
    .in8(pull_resistor_1_node), .in9(pull_resistor_1_node), .in10(pull_resistor_1_node),
    .in11(pull_resistor_1_node), .in12(pull_resistor_1_node), .in13(pull_resistor_1_node),
    .in14(pull_resistor_1_node), .in15(pull_resistor_1_node), .out(Y[2]), .sel(B[3:0]));
  Multiplexer #(.select(4)) multiplexer_15 (
    .in0(A[1]), .in1(A[0]), .in2(pull_resistor_1_node), .in3(pull_resistor_1_node),
    .in4(pull_resistor_1_node), .in5(pull_resistor_1_node), .in6(pull_resistor_1_node),
    .in7(pull_resistor_1_node), .in8(pull_resistor_1_node), .in9(pull_resistor_1_node),
    .in10(pull_resistor_1_node), .in11(pull_resistor_1_node), .in12(pull_resistor_1_node),
    .in13(pull_resistor_1_node), .in14(pull_resistor_1_node), .in15(pull_resistor_1_node), .out(Y[1]),
    .sel(B[3:0]));
  Multiplexer #(.select(4)) multiplexer_16 (
    .in0(A[0]), .in1(pull_resistor_1_node), .in2(pull_resistor_1_node), .in3(pull_resistor_1_node),
    .in4(pull_resistor_1_node), .in5(pull_resistor_1_node), .in6(pull_resistor_1_node),
    .in7(pull_resistor_1_node), .in8(pull_resistor_1_node), .in9(pull_resistor_1_node),
    .in10(pull_resistor_1_node), .in11(pull_resistor_1_node), .in12(pull_resistor_1_node),
    .in13(pull_resistor_1_node), .in14(pull_resistor_1_node), .in15(pull_resistor_1_node), .out(Y[0]),
    .sel(B[3:0]));
  Pull_Resistor pull_resistor_1 (.node(pull_resistor_1_node));
endmodule

module logicshifter (
  input  [15:0] B,
  input  Right,
  input  [15:0] A,
  output [15:0] rY,
  output [15:0] Y
);

  wire pull_resistor_1_node;
  wire [15:0] multiplexer_1_out;

  Multiplexer multiplexer_1 (.in0(A[0]), .in1(A[15]), .out(multiplexer_1_out[0]), .sel(Right));
  Multiplexer multiplexer_2 (.in0(A[1]), .in1(A[14]), .out(multiplexer_1_out[1]), .sel(Right));
  Multiplexer multiplexer_3 (.in0(A[2]), .in1(A[13]), .out(multiplexer_1_out[2]), .sel(Right));
  Multiplexer multiplexer_4 (.in0(A[3]), .in1(A[12]), .out(multiplexer_1_out[3]), .sel(Right));
  Multiplexer multiplexer_5 (.in0(A[4]), .in1(A[11]), .out(multiplexer_1_out[4]), .sel(Right));
  Multiplexer multiplexer_6 (.in0(A[5]), .in1(A[10]), .out(multiplexer_1_out[5]), .sel(Right));
  Multiplexer multiplexer_7 (.in0(A[6]), .in1(A[9]), .out(multiplexer_1_out[6]), .sel(Right));
  Multiplexer multiplexer_8 (.in0(A[7]), .in1(A[8]), .out(multiplexer_1_out[7]), .sel(Right));
  Multiplexer multiplexer_9 (.in0(A[8]), .in1(A[7]), .out(multiplexer_1_out[8]), .sel(Right));
  Multiplexer multiplexer_10 (.in0(A[9]), .in1(A[6]), .out(multiplexer_1_out[9]), .sel(Right));
  Multiplexer multiplexer_11 (.in0(A[10]), .in1(A[5]), .out(multiplexer_1_out[10]), .sel(Right));
  Multiplexer multiplexer_12 (.in0(A[11]), .in1(A[4]), .out(multiplexer_1_out[11]), .sel(Right));
  Multiplexer multiplexer_13 (.in0(A[12]), .in1(A[3]), .out(multiplexer_1_out[12]), .sel(Right));
  Multiplexer multiplexer_14 (.in0(A[13]), .in1(A[2]), .out(multiplexer_1_out[13]), .sel(Right));
  Multiplexer multiplexer_15 (.in0(A[14]), .in1(A[1]), .out(multiplexer_1_out[14]), .sel(Right));
  Multiplexer multiplexer_16 (.in0(A[15]), .in1(A[0]), .out(multiplexer_1_out[15]), .sel(Right));
  Multiplexer #(.select(4)) multiplexer_17 (
    .in0(multiplexer_1_out[15]), .in1(multiplexer_1_out[14]), .in2(multiplexer_1_out[13]),
    .in3(multiplexer_1_out[12]), .in4(multiplexer_1_out[11]), .in5(multiplexer_1_out[10]),
    .in6(multiplexer_1_out[9]), .in7(multiplexer_1_out[8]), .in8(multiplexer_1_out[7]),
    .in9(multiplexer_1_out[6]), .in10(multiplexer_1_out[5]), .in11(multiplexer_1_out[4]),
    .in12(multiplexer_1_out[3]), .in13(multiplexer_1_out[2]), .in14(multiplexer_1_out[1]),
    .in15(multiplexer_1_out[0]), .out(rY[0]), .sel(B[3:0]));
  Multiplexer #(.select(4)) multiplexer_18 (
    .in0(multiplexer_1_out[14]), .in1(multiplexer_1_out[13]), .in2(multiplexer_1_out[12]),
    .in3(multiplexer_1_out[11]), .in4(multiplexer_1_out[10]), .in5(multiplexer_1_out[9]),
    .in6(multiplexer_1_out[8]), .in7(multiplexer_1_out[7]), .in8(multiplexer_1_out[6]),
    .in9(multiplexer_1_out[5]), .in10(multiplexer_1_out[4]), .in11(multiplexer_1_out[3]),
    .in12(multiplexer_1_out[2]), .in13(multiplexer_1_out[1]), .in14(multiplexer_1_out[0]),
    .in15(pull_resistor_1_node), .out(rY[1]), .sel(B[3:0]));
  Multiplexer #(.select(4)) multiplexer_19 (
    .in0(multiplexer_1_out[13]), .in1(multiplexer_1_out[12]), .in2(multiplexer_1_out[11]),
    .in3(multiplexer_1_out[10]), .in4(multiplexer_1_out[9]), .in5(multiplexer_1_out[8]),
    .in6(multiplexer_1_out[7]), .in7(multiplexer_1_out[6]), .in8(multiplexer_1_out[5]),
    .in9(multiplexer_1_out[4]), .in10(multiplexer_1_out[3]), .in11(multiplexer_1_out[2]),
    .in12(multiplexer_1_out[1]), .in13(multiplexer_1_out[0]), .in14(pull_resistor_1_node),
    .in15(pull_resistor_1_node), .out(rY[2]), .sel(B[3:0]));
  Multiplexer #(.select(4)) multiplexer_20 (
    .in0(multiplexer_1_out[12]), .in1(multiplexer_1_out[11]), .in2(multiplexer_1_out[10]),
    .in3(multiplexer_1_out[9]), .in4(multiplexer_1_out[8]), .in5(multiplexer_1_out[7]),
    .in6(multiplexer_1_out[6]), .in7(multiplexer_1_out[5]), .in8(multiplexer_1_out[4]),
    .in9(multiplexer_1_out[3]), .in10(multiplexer_1_out[2]), .in11(multiplexer_1_out[1]),
    .in12(multiplexer_1_out[0]), .in13(pull_resistor_1_node), .in14(pull_resistor_1_node),
    .in15(pull_resistor_1_node), .out(rY[3]), .sel(B[3:0]));
  Multiplexer #(.select(4)) multiplexer_21 (
    .in0(multiplexer_1_out[11]), .in1(multiplexer_1_out[10]), .in2(multiplexer_1_out[9]),
    .in3(multiplexer_1_out[8]), .in4(multiplexer_1_out[7]), .in5(multiplexer_1_out[6]),
    .in6(multiplexer_1_out[5]), .in7(multiplexer_1_out[4]), .in8(multiplexer_1_out[3]),
    .in9(multiplexer_1_out[2]), .in10(multiplexer_1_out[1]), .in11(multiplexer_1_out[0]),
    .in12(pull_resistor_1_node), .in13(pull_resistor_1_node), .in14(pull_resistor_1_node),
    .in15(pull_resistor_1_node), .out(rY[4]), .sel(B[3:0]));
  Multiplexer #(.select(4)) multiplexer_22 (
    .in0(multiplexer_1_out[10]), .in1(multiplexer_1_out[9]), .in2(multiplexer_1_out[8]),
    .in3(multiplexer_1_out[7]), .in4(multiplexer_1_out[6]), .in5(multiplexer_1_out[5]),
    .in6(multiplexer_1_out[4]), .in7(multiplexer_1_out[3]), .in8(multiplexer_1_out[2]),
    .in9(multiplexer_1_out[1]), .in10(multiplexer_1_out[0]), .in11(pull_resistor_1_node),
    .in12(pull_resistor_1_node), .in13(pull_resistor_1_node), .in14(pull_resistor_1_node),
    .in15(pull_resistor_1_node), .out(rY[5]), .sel(B[3:0]));
  Multiplexer #(.select(4)) multiplexer_23 (
    .in0(multiplexer_1_out[9]), .in1(multiplexer_1_out[8]), .in2(multiplexer_1_out[7]),
    .in3(multiplexer_1_out[6]), .in4(multiplexer_1_out[5]), .in5(multiplexer_1_out[4]),
    .in6(multiplexer_1_out[3]), .in7(multiplexer_1_out[2]), .in8(multiplexer_1_out[1]),
    .in9(multiplexer_1_out[0]), .in10(pull_resistor_1_node), .in11(pull_resistor_1_node),
    .in12(pull_resistor_1_node), .in13(pull_resistor_1_node), .in14(pull_resistor_1_node),
    .in15(pull_resistor_1_node), .out(rY[6]), .sel(B[3:0]));
  Multiplexer #(.select(4)) multiplexer_24 (
    .in0(multiplexer_1_out[8]), .in1(multiplexer_1_out[7]), .in2(multiplexer_1_out[6]),
    .in3(multiplexer_1_out[5]), .in4(multiplexer_1_out[4]), .in5(multiplexer_1_out[3]),
    .in6(multiplexer_1_out[2]), .in7(multiplexer_1_out[1]), .in8(multiplexer_1_out[0]),
    .in9(pull_resistor_1_node), .in10(pull_resistor_1_node), .in11(pull_resistor_1_node),
    .in12(pull_resistor_1_node), .in13(pull_resistor_1_node), .in14(pull_resistor_1_node),
    .in15(pull_resistor_1_node), .out(rY[7]), .sel(B[3:0]));
  Multiplexer #(.select(4)) multiplexer_25 (
    .in0(multiplexer_1_out[7]), .in1(multiplexer_1_out[6]), .in2(multiplexer_1_out[5]),
    .in3(multiplexer_1_out[4]), .in4(multiplexer_1_out[3]), .in5(multiplexer_1_out[2]),
    .in6(multiplexer_1_out[1]), .in7(multiplexer_1_out[0]), .in8(pull_resistor_1_node),
    .in9(pull_resistor_1_node), .in10(pull_resistor_1_node), .in11(pull_resistor_1_node),
    .in12(pull_resistor_1_node), .in13(pull_resistor_1_node), .in14(pull_resistor_1_node),
    .in15(pull_resistor_1_node), .out(rY[8]), .sel(B[3:0]));
  Multiplexer #(.select(4)) multiplexer_26 (
    .in0(multiplexer_1_out[6]), .in1(multiplexer_1_out[5]), .in2(multiplexer_1_out[4]),
    .in3(multiplexer_1_out[3]), .in4(multiplexer_1_out[2]), .in5(multiplexer_1_out[1]),
    .in6(multiplexer_1_out[0]), .in7(pull_resistor_1_node), .in8(pull_resistor_1_node),
    .in9(pull_resistor_1_node), .in10(pull_resistor_1_node), .in11(pull_resistor_1_node),
    .in12(pull_resistor_1_node), .in13(pull_resistor_1_node), .in14(pull_resistor_1_node),
    .in15(pull_resistor_1_node), .out(rY[9]), .sel(B[3:0]));
  Multiplexer #(.select(4)) multiplexer_27 (
    .in0(multiplexer_1_out[5]), .in1(multiplexer_1_out[4]), .in2(multiplexer_1_out[3]),
    .in3(multiplexer_1_out[2]), .in4(multiplexer_1_out[1]), .in5(multiplexer_1_out[0]),
    .in6(pull_resistor_1_node), .in7(pull_resistor_1_node), .in8(pull_resistor_1_node),
    .in9(pull_resistor_1_node), .in10(pull_resistor_1_node), .in11(pull_resistor_1_node),
    .in12(pull_resistor_1_node), .in13(pull_resistor_1_node), .in14(pull_resistor_1_node),
    .in15(pull_resistor_1_node), .out(rY[10]), .sel(B[3:0]));
  Multiplexer #(.select(4)) multiplexer_28 (
    .in0(multiplexer_1_out[4]), .in1(multiplexer_1_out[3]), .in2(multiplexer_1_out[2]),
    .in3(multiplexer_1_out[1]), .in4(multiplexer_1_out[0]), .in5(pull_resistor_1_node),
    .in6(pull_resistor_1_node), .in7(pull_resistor_1_node), .in8(pull_resistor_1_node),
    .in9(pull_resistor_1_node), .in10(pull_resistor_1_node), .in11(pull_resistor_1_node),
    .in12(pull_resistor_1_node), .in13(pull_resistor_1_node), .in14(pull_resistor_1_node),
    .in15(pull_resistor_1_node), .out(rY[11]), .sel(B[3:0]));
  Multiplexer #(.select(4)) multiplexer_29 (
    .in0(multiplexer_1_out[3]), .in1(multiplexer_1_out[2]), .in2(multiplexer_1_out[1]),
    .in3(multiplexer_1_out[0]), .in4(pull_resistor_1_node), .in5(pull_resistor_1_node),
    .in6(pull_resistor_1_node), .in7(pull_resistor_1_node), .in8(pull_resistor_1_node),
    .in9(pull_resistor_1_node), .in10(pull_resistor_1_node), .in11(pull_resistor_1_node),
    .in12(pull_resistor_1_node), .in13(pull_resistor_1_node), .in14(pull_resistor_1_node),
    .in15(pull_resistor_1_node), .out(rY[12]), .sel(B[3:0]));
  Multiplexer #(.select(4)) multiplexer_30 (
    .in0(multiplexer_1_out[2]), .in1(multiplexer_1_out[1]), .in2(multiplexer_1_out[0]),
    .in3(pull_resistor_1_node), .in4(pull_resistor_1_node), .in5(pull_resistor_1_node),
    .in6(pull_resistor_1_node), .in7(pull_resistor_1_node), .in8(pull_resistor_1_node),
    .in9(pull_resistor_1_node), .in10(pull_resistor_1_node), .in11(pull_resistor_1_node),
    .in12(pull_resistor_1_node), .in13(pull_resistor_1_node), .in14(pull_resistor_1_node),
    .in15(pull_resistor_1_node), .out(rY[13]), .sel(B[3:0]));
  Multiplexer #(.select(4)) multiplexer_31 (
    .in0(multiplexer_1_out[1]), .in1(multiplexer_1_out[0]), .in2(pull_resistor_1_node),
    .in3(pull_resistor_1_node), .in4(pull_resistor_1_node), .in5(pull_resistor_1_node),
    .in6(pull_resistor_1_node), .in7(pull_resistor_1_node), .in8(pull_resistor_1_node),
    .in9(pull_resistor_1_node), .in10(pull_resistor_1_node), .in11(pull_resistor_1_node),
    .in12(pull_resistor_1_node), .in13(pull_resistor_1_node), .in14(pull_resistor_1_node),
    .in15(pull_resistor_1_node), .out(rY[14]), .sel(B[3:0]));
  Multiplexer #(.select(4)) multiplexer_32 (
    .in0(multiplexer_1_out[0]), .in1(pull_resistor_1_node), .in2(pull_resistor_1_node),
    .in3(pull_resistor_1_node), .in4(pull_resistor_1_node), .in5(pull_resistor_1_node),
    .in6(pull_resistor_1_node), .in7(pull_resistor_1_node), .in8(pull_resistor_1_node),
    .in9(pull_resistor_1_node), .in10(pull_resistor_1_node), .in11(pull_resistor_1_node),
    .in12(pull_resistor_1_node), .in13(pull_resistor_1_node), .in14(pull_resistor_1_node),
    .in15(pull_resistor_1_node), .out(rY[15]), .sel(B[3:0]));
  Pull_Resistor pull_resistor_1 (.node(pull_resistor_1_node));

  assign Y = {rY[0], rY[1], rY[2], rY[3], rY[4], rY[5], rY[6], rY[7], rY[8], rY[9], rY[10], rY[11], rY[12], rY[13], rY[14], rY[15]};
endmodule

module aluMICROCODED (
  input  [3:0] OP,
  input  CLK,
  input  [15:0] Din,
  output FS,
  output FO,
  output FC,
  output FZ,
  output [15:0] Dout
);

  wire alu_1_fc, alu_1_fo, alu_1_fs, alu_1_fz, and_1_out, pull_resistor_1_node, pull_resistor_2_node,
       xor_1_out;
  wire [15:0] register_1_q, register_2_q;

  xor xor_1 (xor_1_out, OP[0], OP[3]);
  and and_1 (and_1_out, OP[0], OP[3]);
  Register #(.trigger("falling"), .width(16)) register_1 (
    .D(Din), .en(xor_1_out), .clk(CLK), .Q(register_1_q), .clr(pull_resistor_1_node));
  Register #(.trigger("falling"), .width(16)) register_2 (
    .D(Din), .en(and_1_out), .clk(CLK), .Q(register_2_q), .clr(pull_resistor_1_node));
  Pull_Resistor pull_resistor_1 (.node(pull_resistor_1_node));
  alu alu_1 (
    .funct(OP[2:0]), .A(register_1_q), .B(register_2_q), .Y(Dout), .FZ(alu_1_fz), .FO(alu_1_fo),
    .FC(alu_1_fc), .FS(alu_1_fs));
  D_Flip_Flop d_ff_1 (.D(alu_1_fs), .clk(CLK), .Q(FS), .reset(pull_resistor_2_node));  // open: Qn, preset
  D_Flip_Flop d_ff_2 (.D(alu_1_fo), .clk(CLK), .Q(FO), .reset(pull_resistor_2_node));  // open: Qn, preset
  D_Flip_Flop d_ff_3 (.D(alu_1_fc), .clk(CLK), .Q(FC), .reset(pull_resistor_2_node));  // open: Qn, preset
  D_Flip_Flop d_ff_4 (.D(alu_1_fz), .clk(CLK), .Q(FZ), .reset(pull_resistor_2_node));  // open: Qn, preset
  Pull_Resistor pull_resistor_2 (.node(pull_resistor_2_node));
endmodule
