// Logisim project master.circ as structural Verilog: 6 circuits, main circuit main
module main (
);

  wire alu_1_fc, alu_1_fo, alu_1_fs, alu_1_fz, clock_1_out, clock_2_out, clock_3_out, clock_4_out,
       clock_5_out, clock_6_out, clock_7_out, control_1_mask_restore, control_1_mask_save, control_1_oint,
       control_1_oregwe, io_1_ogpu_clear, io_1_okeyread, keyboard_1_avail, memory_controller_1_gpu_we,
       registerfile_1_busy, registerfile_1_int;
  wire [1:0] control_1_oioop;
  wire [2:0] control_1_ointid, control_1_oioaddr, control_1_omemop, registerfile_1_int_id;
  wire [3:0] control_1_oaluop, control_1_oregid;
  wire [6:0] keyboard_1_data, memory_controller_1_gpu_data;
  wire [7:0] io_1_obusyassert, io_1_ointasssert;
  wire [15:0] alu_1_busout, control_1_oiobus, control_1_oregbus, io_1_oled, memory_controller_1_databusout;
  wire [15:7] memory_controller_1_gpu_data_2;

  Clock clock_1 (.out(clock_1_out));
  TTY tty_1 (
    .data(memory_controller_1_gpu_data), .clk(clock_1_out), .we(memory_controller_1_gpu_we),
    .clr(io_1_ogpu_clear));
  Clock clock_2 (.out(clock_2_out));
  memory_controller memory_controller_1 (
    .MODE(control_1_omemop), .DataBUSin(memory_controller_1_databusout), .CLK(clock_2_out),
    .GPU_DATA({memory_controller_1_gpu_data_2, memory_controller_1_gpu_data}),
    .GPU_WE(memory_controller_1_gpu_we), .DataBUSout(memory_controller_1_databusout));  // open: GPU_ADDR
  Clock clock_3 (.out(clock_3_out));
  Clock clock_4 (.out(clock_4_out));
  alu alu_1 (
    .op(control_1_oaluop), .busin(alu_1_busout), .clk(clock_4_out), .busout(alu_1_busout), .FC(alu_1_fc),
    .FS(alu_1_fs), .FZ(alu_1_fz), .FO(alu_1_fo));
  control control_1 (
    .ialubus(alu_1_busout), .ifs(alu_1_fs), .ifo(alu_1_fo), .ifc(alu_1_fc), .ifz(alu_1_fz),
    .imembus(memory_controller_1_databusout), .iregbus(control_1_oregbus), .iint(registerfile_1_int),
    .iintid(registerfile_1_int_id), .ibusy(registerfile_1_busy), .iiobus(control_1_oiobus),
    .CLK(clock_3_out), .oregwe(control_1_oregwe), .omemop(control_1_omemop), .oioaddr(control_1_oioaddr),
    .ointid(control_1_ointid), .oint(control_1_oint), .oaluop(control_1_oaluop), .oalubus(alu_1_busout),
    .omembus(memory_controller_1_databusout), .oregbus(control_1_oregbus), .oregid(control_1_oregid),
    .mask_save(control_1_mask_save), .mask_restore(control_1_mask_restore), .oiobus(control_1_oiobus),
    .oioop(control_1_oioop));
  IO io_1 (
    .ikeychar(keyboard_1_data), .ikeyaval(keyboard_1_avail), .CLK(clock_7_out), .iioid(control_1_oioaddr),
    .iiocmd(control_1_oioop), .iiobus(control_1_oiobus), .iint(control_1_oint), .iintid(control_1_ointid),
    .obusyassert(io_1_obusyassert), .ogpu_clear(io_1_ogpu_clear), .okeyread(io_1_okeyread), .oled(io_1_oled),
    .oiobus(control_1_oiobus), .ointasssert(io_1_ointasssert));
  Clock clock_5 (.out(clock_5_out));
  Keyboard keyboard_1 (
    .clk(clock_5_out), .re(io_1_okeyread), .clr(1'b0), .avail(keyboard_1_avail), .data(keyboard_1_data));
  Clock clock_6 (.out(clock_6_out));
  Clock clock_7 (.out(clock_7_out));
  registerfile registerfile_1 (
    .regid(control_1_oregid), .mask_restore(control_1_mask_restore), .CLK(clock_6_out),
    .wr_enable(control_1_oregwe), .mask_save(control_1_mask_save), .data_in(control_1_oregbus),
    .ioint(io_1_ointasssert), .iobusy(io_1_obusyassert), .INT_ID(registerfile_1_int_id),
    .INT(registerfile_1_int), .BUSY(registerfile_1_busy), .data_out(control_1_oregbus));
  // LedBar #(.inputtype("row"), .matrixcols(16)) ledbar_1: pin names not known; wires that end beside it: io_1_oled
endmodule

module memory_controller (
  input  [15:0] DataBUSin,
  input  [2:0] MODE,
  input  CLK,
  output [14:0] GPU_ADDR,
  output [15:0] GPU_DATA,
  output GPU_WE,
  output [15:0] DataBUSout
);

  wire and_3_out, not_1_out, output_enable, write_enable;
  wire [15:0] adder_1_out, general_purpose_memory_dout, multiplexer_1_out, multiplexer_2_out, rom_1_data;
  wire [15:15] RegAddr_q;

  not not_1 (not_1_out, output_enable);
  assign GPU_DATA = not_1_out ? DataBUSin : 16'bz;  // Controlled_Buffer controlled_buffer_1
  and and_1 (write_enable, MODE[2], ~MODE[1], ~MODE[0]);  // AND_Gate
  and and_2 (output_enable, MODE[2], MODE[0]);
  Multiplexer #(.width(16)) multiplexer_1 (.in0(GPU_DATA), .in1(adder_1_out), .out(multiplexer_1_out), .sel(MODE[0]));
  Register #(.width(16)) RegAddr (
    .D(multiplexer_1_out), .en(MODE[1]), .clk(CLK), .Q({RegAddr_q[15], GPU_ADDR}));  // open: clr
  Adder #(.width(16)) adder_1 (.a({RegAddr_q[15], GPU_ADDR}), .b(16'h1), .out(adder_1_out));  // open: cin, cout
  and and_3 (and_3_out, RegAddr_q[15], write_enable);
  ROM #(.addrWidth(16), .dataWidth(16)) rom_1 (.addr({RegAddr_q[15], GPU_ADDR}), .data(rom_1_data));
  RAM #(.addrWidth(16), .asyncread("true"), .dataWidth(16), .\type ("nonvolatile")) general_purpose_memory (
    .addr({RegAddr_q[15], GPU_ADDR}), .we(and_3_out), .oe(1'b1), .clk(CLK), .din(GPU_DATA),
    .dout(general_purpose_memory_dout));
  and and_4 (GPU_WE, ~RegAddr_q[15], write_enable);  // AND_Gate
  Multiplexer #(.width(16)) multiplexer_2 (
    .in0(rom_1_data), .in1(general_purpose_memory_dout), .out(multiplexer_2_out), .sel(RegAddr_q[15]));
  assign DataBUSout = output_enable ? multiplexer_2_out : 16'bz;  // Controlled_Buffer controlled_buffer_2

  // Other names for the same wires on the sheet: Data_in[15:0] = GPU_DATA

  // Notes on the sheet:
  //   15 bit
  //   contents of rom_1 (hex, n*v repeats v):
  //   2b10 4000 1810 ff00 8880 fecf 2880 1 9880 fecf d080 b100 c004 c005 c008 6140 8850 feff 1084 a800 44
  //   3940 a 4900 28 3940 8 4900 34 9045 2850 1 2b50 ff00 9850 feff d080 d050 d040 b100 1850 ff00 9850
  //   feff 1880 1 9880 fefe d080 d050 d040 b100 3950 ff00 4900 3f 2950 1 1840 20 9045 9850 feff d080 d050
  //   d040 b100 0 8890 feef 3980 a 4900 56 3980 8 4900 5d 9089 2890 1 2a90 7fff 9890 feef b000 2890 100
  //   2a90 7f00 9890 feef b000 2990 1 2a90 7fff 9890 feef 1880 20 9089 b000 3299 4900 77 c008 c009 8088
  //   a800 44 d090 d080 2880 1 2990 1 4800 67 b000 a800 67 1880 a 4800 44 c004 1048 1880 78 a800 44 1084
  //   2f80 c 2a80 f 2880 fed0 8088 a800 44 1084 2f80 8 2a80 f 2880 fed0 8088 a800 44 1084 2f80 4 2a80 f
  //   2880 fed0 8088 a800 44 1084 2f80 0 2a80 f 2880 fed0 8088 a800 44 d040 b000 3288 4900 b8 1880 f000
  //   1890 4 a800 67 b000 1880 f004 1890 5 a800 67 b000 1880 7fff 1890 20 9098 2980 1 4a00 c3 9098 9880
  //   feef b000 32aa 4900 dc 80b8 80c9 31bc 4a00 df 2880 1 2890 1 29a0 1 4800 cc 1880 1 b000 1880 0 b000
  //   1820 f000 5900 e4 7800 0 5900 e8 7800 2 5900 ec 7800 1 5900 f0 7800 c 5900 f4 7800 2 5900 f8 7800 43
  //   5900 fc 7800 3 5900 100 7800 43 5900 104 7800 4 5900 108 7800 43 5900 10c 7800 5 5900 110 7800 43
  //   5900 114 7800 6 5900 118 7800 43 5900 11c 7800 7 5900 120 7800 43 1880 f009 1890 b a800 78 2b10 8000
  //   2b10 4000 1880 3e a800 44 1880 20 9880 ff00 9880 ff01 9880 ff02 9880 ff03 9880 ff04 9880 ff05 9880
  //   ff06 9880 ff07 9880 ff08 9880 ff09 9880 ff0a 9880 ff0b 9880 ff0c 9880 ff0d 9880 ff0e 9880 ff0f 9880
  //   ff10 9880 ff11 9880 ff12 9880 ff13 9880 ff14 9880 ff15 9880 ff16 9880 ff17 9880 ff18 9880 ff19 9880
  //   ff1a 9880 ff1b 9880 ff1c 9880 ff1d 9880 ff1e 9880 ff1f 9880 ff20 9880 ff21 9880 ff22 9880 ff23 9880
  //   ff24 9880 ff25 9880 ff26 9880 ff27 9880 ff28 9880 ff29 9880 ff2a 9880 ff2b 9880 ff2c 9880 ff2d 9880
  //   ff2e 9880 ff2f 9880 ff30 9880 ff31 9880 ff32 9880 ff33 9880 ff34 9880 ff35 9880 ff36 9880 ff37 9880
  //   ff38 9880 ff39 9880 ff3a 9880 ff3b 9880 ff3c 9880 ff3d 9880 ff3e 9880 ff3f 9880 ff40 9880 ff41 9880
  //   ff42 9880 ff43 9880 ff44 9880 ff45 9880 ff46 9880 ff47 9880 ff48 9880 ff49 9880 ff4a 9880 ff4b 9880
  //   ff4c 9880 ff4d 9880 ff4e 9880 ff4f 9880 ff50 9880 ff51 9880 ff52 9880 ff53 9880 ff54 9880 ff55 9880
  //   ff56 9880 ff57 9880 ff58 9880 ff59 9880 ff5a 9880 ff5b 9880 ff5c 9880 ff5d 9880 ff5e 9880 ff5f 9880
  //   ff60 9880 ff61 9880 ff62 9880 ff63 9880 ff64 9880 ff65 9880 ff66 9880 ff67 9880 ff68 9880 ff69 9880
  //   ff6a 9880 ff6b 9880 ff6c 9880 ff6d 9880 ff6e 9880 ff6f 9880 ff70 9880 ff71 9880 ff72 9880 ff73 9880
  //   ff74 9880 ff75 9880 ff76 9880 ff77 9880 ff78 9880 ff79 9880 ff7a 9880 ff7b 9880 ff7c 9880 ff7d 9880
  //   ff7e 9880 ff7f 9880 ff80 9880 ff81 9880 ff82 9880 ff83 9880 ff84 9880 ff85 9880 ff86 9880 ff87 9880
  //   ff88 9880 ff89 9880 ff8a 9880 ff8b 9880 ff8c 9880 ff8d 9880 ff8e 9880 ff8f 9880 ff90 9880 ff91 9880
  //   ff92 9880 ff93 9880 ff94 9880 ff95 9880 ff96 9880 ff97 9880 ff98 9880 ff99 9880 ff9a 9880 ff9b 9880
  //   ff9c 9880 ff9d 9880 ff9e 9880 ff9f 9880 ffa0 9880 ffa1 9880 ffa2 9880 ffa3 9880 ffa4 9880 ffa5 9880
  //   ffa6 9880 ffa7 9880 ffa8 9880 ffa9 9880 ffaa 9880 ffab 9880 ffac 9880 ffad 9880 ffae 9880 ffaf 9880
  //   ffb0 9880 ffb1 9880 ffb2 9880 ffb3 9880 ffb4 9880 ffb5 9880 ffb6 9880 ffb7 9880 ffb8 9880 ffb9 9880
  //   ffba 9880 ffbb 9880 ffbc 9880 ffbd 9880 ffbe 9880 ffbf 9880 ffc0 9880 ffc1 9880 ffc2 9880 ffc3 9880
  //   ffc4 9880 ffc5 9880 ffc6 9880 ffc7 9880 ffc8 9880 ffc9 9880 ffca 9880 ffcb 9880 ffcc 9880 ffcd 9880
  //   ffce 9880 ffcf 9880 ffd0 9880 ffd1 9880 ffd2 9880 ffd3 9880 ffd4 9880 ffd5 9880 ffd6 9880 ffd7 9880
  //   ffd8 9880 ffd9 9880 ffda 9880 ffdb 9880 ffdc 9880 ffdd 9880 ffde 9880 ffdf 9880 ffe0 9880 ffe1 9880
  //   ffe2 9880 ffe3 9880 ffe4 9880 ffe5 9880 ffe6 9880 ffe7 9880 ffe8 9880 ffe9 9880 ffea 9880 ffeb 9880
  //   ffec 9880 ffed 9880 ffee 9880 ffef 9880 fff0 9880 fff1 9880 fff2 9880 fff3 9880 fff4 9880 fff5 9880
  //   fff6 9880 fff7 9880 fff8 9880 fff9 9880 fffa 9880 fffb 9880 fffc 9880 fffd 9880 fffe 9880 ffff 8840
  //   fefe 3244 4900 334 1840 0 9840 fefe 1880 ff00 1890 f018 18a0 4 a800 cc 3288 4a00 371 1880 ff00 1890
  //   f084 18a0 4 a800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
  //   VRAM
  //   ROM
  //   RAM
endmodule

module control (
  input  CLK,
  input  [15:0] ialubus,
  input  ifs,
  input  ifo,
  input  ifc,
  input  ifz,
  input  [15:0] imembus,
  input  [15:0] iregbus,
  input  iint,
  input  [2:0] iintid,
  input  ibusy,
  input  [15:0] iiobus,
  output [3:0] oaluop,
  output [15:0] oalubus,
  output [2:0] omemop,
  output [15:0] omembus,
  output oregwe,
  output [15:0] oregbus,
  output [3:0] oregid,
  output mask_save,
  output mask_restore,
  output [1:0] oioop,
  output [15:0] oiobus,
  output [2:0] oioaddr,
  output [2:0] ointid,
  output oint
);

  wire and_1_out, and_2_out, and_3_out, and_4_out, and_5_out, and_8_out, c, flwe, instr_load, isimm, isint,
       isjump, isret, isstack, next_instr, not_1_out, not_2_out, not_3_out, not_4_out, not_5_out, not_6_out,
       o, or_1_out, or_2_out, or_3_out, regds, regsrc, s, should_jump, tempregwe, valid, xnor_1_out,
       xnor_2_out, xor_1_out, xor_2_out, z;
  wire [1:0] alumode, alusrc, ioop, memsrc;
  wire [2:0] funct;
  wire [3:0] adder_2_out, cycle, flags_saved, multiplexer_7_out, multiplexer_10_out, multiplexer_11_out,
       opcode;
  wire [7:0] instruction_q;
  wire [15:0] alubus, alubuswrite, iobuswrite, ip, ipnext, membus, membuswrite, multiplexer_1_out,
       multiplexer_2_out, multiplexer_3_out, multiplexer_4_out, multiplexer_12_out, multiplexer_17_out,
       regbuswrite, srctempbus, tempreg;
  wire [23:22] rom_1_data;

  Adder #(.width(16)) adder_1 (.a(ip), .b(16'h1), .out(ipnext), .cin(isimm));  // open: cout
  Multiplexer #(.width(16)) multiplexer_1 (.in0(ipnext), .in1(iobuswrite), .out(multiplexer_1_out), .sel(and_1_out));
  and and_1 (and_1_out, isjump, should_jump);
  not not_1 (not_1_out, oaluop[3]);
  assign alubus = not_1_out ? ialubus : 16'bz;  // Controlled_Buffer controlled_buffer_1
  assign membus = and_5_out ? imembus : 16'bz;  // Controlled_Buffer controlled_buffer_2
  Multiplexer #(.width(16)) multiplexer_2 (.in0(membus), .in1({16{1'b0}}), .out(multiplexer_2_out), .sel(isint));
  Multiplexer #(.width(16)) multiplexer_3 (.in0(multiplexer_1_out), .in1(membus), .out(multiplexer_3_out), .sel(isret));
  Multiplexer #(.width(16)) multiplexer_4 (.in0(multiplexer_3_out), .in1(iiobus), .out(multiplexer_4_out), .sel(isint));
  Register #(.width(16)) instruction (
    .D(multiplexer_2_out), .en(instr_load), .clk(CLK), .Q({opcode, isimm, funct, instruction_q}), .clr(1'b0));
  Register #(.width(16)) u_IP (.D(multiplexer_4_out), .en(next_instr), .clk(CLK), .Q(ip), .clr(1'b0));
  xnor xnor_1 (xnor_1_out, s, o);
  xor xor_1 (xor_1_out, s, o);
  xnor xnor_2 (xnor_2_out, s, o);
  xor xor_2 (xor_2_out, s, o);
  Clock clock_1 ();  // open: out
  and and_2 (and_2_out, ioop[0], ioop[1]);
  Pull_Resistor pull_resistor_1 (.node({opcode, isimm, funct, instruction_q}));
  not not_2 (not_2_out, z);
  or or_1 (or_1_out, z, xor_1_out);
  and and_3 (and_3_out, ~z, xnor_2_out);  // AND_Gate
  not not_3 (not_3_out, s);
  not not_4 (not_4_out, c);
  or or_2 (or_2_out, c, z);
  and and_4 (and_4_out, ~c, ~z);  // AND_Gate
  not not_5 (not_5_out, o);
  assign oalubus = oaluop[3] ? alubuswrite : 16'bz;  // Controlled_Buffer controlled_buffer_3
  and and_5 (and_5_out, omemop[0], omemop[2]);
  not not_6 (not_6_out, and_5_out);
  assign omembus = not_6_out ? membuswrite : 16'bz;  // Controlled_Buffer controlled_buffer_4
  assign oregbus = oregwe ? regbuswrite : 16'bz;  // Controlled_Buffer controlled_buffer_5
  assign oiobus = and_2_out ? iobuswrite : 16'bz;  // Controlled_Buffer controlled_buffer_6
  Multiplexer #(.width(3)) multiplexer_5 (.in0(funct), .in1(3'b000), .out(oioaddr), .sel(isint));
  Multiplexer #(.width(2)) multiplexer_6 (.in0(ioop), .in1(2'b10), .out(oioop), .sel(isint));
  Multiplexer #(.width(4)) multiplexer_7 (
    .in0(instruction_q[7:4]), .in1(instruction_q[3:0]), .out(multiplexer_7_out), .sel(regds));
  Multiplexer #(.select(4)) multiplexer_8 (
    .in0(1'b1), .in1(z), .in2(not_2_out), .in3(xnor_1_out), .in4(or_1_out), .in5(and_3_out), .in6(xor_2_out),
    .in7(o), .in8(ibusy), .in9(s), .in10(not_3_out), .in11(not_4_out), .in12(or_2_out), .in13(and_4_out),
    .in14(c), .in15(not_5_out), .out(should_jump), .sel({opcode[0], funct}));
  Multiplexer #(.width(4)) multiplexer_9 (.in0(multiplexer_7_out), .in1(4'b0010), .out(oregid), .sel(isstack));
  Adder #(.width(4)) adder_2 (.a(cycle), .b(4'b0001), .out(adder_2_out));  // open: cin, cout
  Register #(.width(4)) u_cycle (.D(multiplexer_10_out), .en(1'b1), .clk(CLK), .Q(cycle), .clr(1'b0));
  Multiplexer #(.width(4)) multiplexer_10 (
    .in0(adder_2_out), .in1(4'b0000), .out(multiplexer_10_out), .sel(next_instr));
  Register #(.width(4)) flags (.D(multiplexer_11_out), .en(or_3_out), .clk(CLK), .Q({z, c, o, s}), .clr(1'b0));
  Multiplexer #(.width(4)) multiplexer_11 (
    .in0({ifz, ifc, ifo, ifs}), .in1(flags_saved), .out(multiplexer_11_out), .sel(mask_restore));
  or or_3 (or_3_out, mask_restore, flwe);
  Register #(.width(16)) u_tempreg (.D(membus), .en(tempregwe), .clk(CLK), .Q(tempreg), .clr(1'b0));
  ROM #(.dataWidth(24)) rom_1 (
    .addr({opcode, cycle}),
    .data({rom_1_data, ioop, isret, isstack, tempregwe, isjump, flwe, omemop, memsrc, instr_load, regsrc, oregwe, regds, alusrc, alumode, valid, next_instr}));
  Pull_Resistor pull_resistor_2 (.node(cycle));
  Pull_Resistor pull_resistor_3 (.node({rom_1_data, ioop, isret, isstack, tempregwe, isjump, flwe, omemop, memsrc, instr_load, regsrc, oregwe, regds, alusrc, alumode, valid, next_instr}));
  Register #(.width(4)) flags_int (.D({z, c, o, s}), .en(mask_save), .clk(CLK), .Q(flags_saved), .clr(1'b0));
  Register #(.width(1)) register_1 (.D(iint), .en(next_instr), .clk(CLK), .Q(isint), .clr(1'b0));
  and and_6 (mask_save, iint, next_instr);
  and and_7 (mask_restore, isret, next_instr, funct[0]);
  Multiplexer #(.width(16)) multiplexer_12 (.in0(ip), .in1(ipnext), .out(multiplexer_12_out), .sel(isjump));
  Multiplexer #(.width(16)) multiplexer_13 (.in0(iregbus), .in1(membus), .out(iobuswrite), .sel(isimm));
  Multiplexer #(.width(16)) multiplexer_14 (.in0(iregbus), .in1(tempreg), .out(srctempbus), .sel(isimm));
  Multiplexer #(.select(2), .width(4)) multiplexer_15 (
    .in0({1'b0, funct}), .in1({3'b100, regds}), .in2(4'b0000), .in3(4'b0001), .out(oaluop), .sel(alumode));
  Multiplexer #(.select(2), .width(16)) multiplexer_16 (
    .in0(iregbus), .in1(iobuswrite), .in2({16{1'b0}}), .in3(16'h1), .out(alubuswrite), .sel(alusrc));
  Multiplexer #(.width(16)) multiplexer_17 (.in0(alubus), .in1(membus), .out(multiplexer_17_out), .sel(regsrc));
  Multiplexer #(.select(2), .width(16)) multiplexer_18 (
    .in0(iregbus), .in1(iobuswrite), .in2(multiplexer_12_out), .in3(srctempbus), .out(membuswrite),
    .sel(memsrc));
  and and_8 (and_8_out, ~ioop[0], ioop[1]);  // AND_Gate
  Multiplexer #(.width(16)) multiplexer_19 (.in0(multiplexer_17_out), .in1(iiobus), .out(regbuswrite), .sel(and_8_out));

  assign oint = mask_save;
  assign ointid = iintid;

  // Other names for the same wires on the sheet: fs = ifs; fo = ifo; fc = ifc; fz = ifz; regwe = oregwe;
  //   memop[2:0] = omemop; aluop[3:0] = oaluop; busy = ibusy; enter_int = mask_save; int = iint; intid[2:0] = iintid;
  //   iobus[15:0] = iiobus; leave_int = mask_restore; regbus[15:0] = iregbus; regid[3:0] = oregid;
  //   srcbus[15:0] = iobuswrite

  // Notes on the sheet:
  //   MEM
  //   REG
  //   IO
  //   ALU
  //   REGISTERS
  //   JUMPS
  //   contents of rom_1 (hex, n*v repeats v):
  //   2802 7202 40004 25074 4208c 4841 10*1 2802 7202 26 5056 8b 11*1 2802 7202 6 5056 8083 11*1 2802 7202
  //   6 5056 8003 11*1 2802 7202 15043 13*1 2802 7202 15043 13*1 2802 7202 200083 13*1 2802 7202 305043
  //   13*1 2802 7202 25002 2c42 5183 11*1 2802 7202 25002 2c42 4003 11*1 2802 7202 40006 25076 4208e 14802
  //   2802 3002 15103 7*1 2802 7202 42006 76 c508b 11*1 2802 7202 40006 25076 4208e 4c43 10*1 2802 7202
  //   42006 76 4008a 5183 10*1 2802 7202 14*1 2802 7202 14*1
  //   CONTROL SIGNALS
  //   BUSES
endmodule

module alu (
  input  clk,
  input  [15:0] busin,
  input  [3:0] op,
  output [15:0] busout,
  output FC,
  output FS,
  output FZ,
  output FO
);

  wire adder_1_cout, and_1_out, and_2_out, comparator_1_eq, comparator_2_eq, out_enable, subtractor_1_bout,
       xnor_1_out, xor_1_out;
  wire [14:0] aluout;
  wire [15:0] A, adder_1_out, and_4_out, B, not_2_out, or_1_out, shifter_1_out, shifter_2_out,
       subtractor_1_out, xor_2_out;

  Comparator #(.width(3)) comparator_1 (.a(op[2:0]), .b(3'b000), .eq(comparator_1_eq));  // open: gt, lt
  Comparator #(.width(3)) comparator_2 (.a(op[2:0]), .b(3'b001), .eq(comparator_2_eq));  // open: gt, lt
  not not_1 (out_enable, op[3]);
  and and_1 (and_1_out, op[3], comparator_1_eq);
  and and_2 (and_2_out, op[3], comparator_2_eq);
  Register #(.width(16)) register_1 (.D(busin), .en(and_1_out), .clk(clk), .Q(A), .clr(1'b0));
  Register #(.width(16)) register_2 (.D(busin), .en(and_2_out), .clk(clk), .Q(B), .clr(1'b0));
  assign busout = out_enable ? {FS, aluout} : 16'bz;  // Controlled_Buffer controlled_buffer_1
  Comparator #(.width(16)) comparator_3 (.a({FS, aluout}), .b({16{1'b0}}), .eq(FZ));  // open: gt, lt
  xnor xnor_1 (xnor_1_out, FS, B[15]);
  xor xor_1 (xor_1_out, A[15], B[15]);
  and and_3 (FO, xnor_1_out, xor_1_out);
  Adder #(.width(16)) adder_1 (.a(A), .b(B), .out(adder_1_out), .cin(1'b0), .cout(adder_1_cout));
  Subtractor #(.width(16)) subtractor_1 (.a(A), .b(B), .out(subtractor_1_out), .bin(1'b0), .bout(subtractor_1_bout));
  assign and_4_out = A & B;  // AND_Gate and_4, 16 bits wide
  assign or_1_out = A | B;  // OR_Gate or_1, 16 bits wide
  assign xor_2_out = A ^ B;  // XOR_Gate xor_2, 16 bits wide
  assign not_2_out = ~A;  // NOT_Gate not_2, 16 bits wide
  Shifter #(.width(16)) shifter_1 (.in(A), .\dist (B[3:0]), .out(shifter_1_out));
  Shifter #(.shift("lr"), .width(16)) shifter_2 (.in(A), .\dist (B[3:0]), .out(shifter_2_out));
  Multiplexer #(.select(3)) multiplexer_1 (
    .in0(adder_1_cout), .in1(subtractor_1_bout), .in2(1'b0), .in3(1'b0), .in4(1'b0), .in5(1'b0), .in6(1'b0),
    .in7(1'b0), .out(FC), .sel(op[2:0]));
  Multiplexer #(.select(3), .width(16)) multiplexer_2 (
    .in0(adder_1_out), .in1(subtractor_1_out), .in2(and_4_out), .in3(or_1_out), .in4(xor_2_out),
    .in5(not_2_out), .in6(shifter_1_out), .in7(shifter_2_out), .out({FS, aluout}), .sel(op[2:0]));

  // Other names for the same wires on the sheet: aluout[15] = FS; bin[15:0] = busin; cout = FC; aluop[2:0] = op[2:0];
  //   regid[2:0] = op[2:0]; regwe = op[3]
endmodule

module registerfile (
  input  [7:0] ioint,
  input  CLK,
  input  [15:0] data_in,
  input  [7:0] iobusy,
  input  wr_enable,
  input  mask_save,
  input  mask_restore,
  input  [3:0] regid,
  output [2:0] INT_ID,
  output INT,
  output BUSY,
  output [15:0] data_out
);

  wire demultiplexer_1_out0, demultiplexer_1_out2, demultiplexer_1_out3, demultiplexer_1_out4,
       demultiplexer_1_out5, demultiplexer_1_out6, demultiplexer_1_out7, demultiplexer_1_out8,
       demultiplexer_1_out9, demultiplexer_1_out10, demultiplexer_1_out11, demultiplexer_1_out12,
       demultiplexer_1_out13, demultiplexer_1_out14, demultiplexer_1_out15, not_1_out, or_1_out, r1we;
  wire [7:0] and_1_out;
  wire [15:0] mask_saved, multiplexer_1_out, multiplexer_2_out, multiplexer_3_out, multiplexer_4_out, r0_out,
       r1_out, r2_q, r3_q, r4_q, r5_q, r6_q, r7_q, r8_q, r9_q, r10_q, r11_q, r12_q, r13_q, r14_q, r15_q;

  Demultiplexer #(.select(4)) demultiplexer_1 (
    .out0(demultiplexer_1_out0), .out1(r1we), .out2(demultiplexer_1_out2), .out3(demultiplexer_1_out3),
    .out4(demultiplexer_1_out4), .out5(demultiplexer_1_out5), .out6(demultiplexer_1_out6),
    .out7(demultiplexer_1_out7), .out8(demultiplexer_1_out8), .out9(demultiplexer_1_out9),
    .out10(demultiplexer_1_out10), .out11(demultiplexer_1_out11), .out12(demultiplexer_1_out12),
    .out13(demultiplexer_1_out13), .out14(demultiplexer_1_out14), .out15(demultiplexer_1_out15),
    .in(wr_enable), .sel(regid));
  Multiplexer #(.width(16)) multiplexer_1 (.in0(r1_out), .in1(data_in), .out(multiplexer_1_out), .sel(r1we));
  Register #(.width(16)) mask_storage (.D(multiplexer_1_out), .en(mask_save), .clk(CLK), .Q(mask_saved));  // open: clr
  Multiplexer #(.width(16)) multiplexer_2 (
    .in0(data_in), .in1(mask_saved), .out(multiplexer_2_out), .sel(mask_restore));
  Multiplexer #(.width(16)) multiplexer_3 (
    .in0(multiplexer_2_out), .in1({16{1'b0}}), .out(multiplexer_3_out), .sel(mask_save));
  or or_1 (or_1_out, r1we, mask_save, mask_restore);
  Register #(.width(16)) r0 (.D({ioint, iobusy}), .en(1'b1), .clk(CLK), .Q(r0_out));  // open: clr
  Register #(.width(16)) r1 (.D(multiplexer_3_out), .en(or_1_out), .clk(CLK), .Q(r1_out));  // open: clr
  Register #(.width(16)) r2 (.D(data_in), .en(demultiplexer_1_out2), .clk(CLK), .Q(r2_q));  // open: clr
  Register #(.width(16)) r3 (.D(data_in), .en(demultiplexer_1_out3), .clk(CLK), .Q(r3_q));  // open: clr
  Register #(.width(16)) r4 (.D(data_in), .en(demultiplexer_1_out4), .clk(CLK), .Q(r4_q));  // open: clr
  Register #(.width(16)) r5 (.D(data_in), .en(demultiplexer_1_out5), .clk(CLK), .Q(r5_q));  // open: clr
  Register #(.width(16)) r6 (.D(data_in), .en(demultiplexer_1_out6), .clk(CLK), .Q(r6_q));  // open: clr
  Register #(.width(16)) r7 (.D(data_in), .en(demultiplexer_1_out7), .clk(CLK), .Q(r7_q));  // open: clr
  Register #(.width(16)) r8 (.D(data_in), .en(demultiplexer_1_out8), .clk(CLK), .Q(r8_q));  // open: clr
  Register #(.width(16)) r9 (.D(data_in), .en(demultiplexer_1_out9), .clk(CLK), .Q(r9_q));  // open: clr
  Register #(.width(16)) r10 (.D(data_in), .en(demultiplexer_1_out10), .clk(CLK), .Q(r10_q));  // open: clr
  Register #(.width(16)) r11 (.D(data_in), .en(demultiplexer_1_out11), .clk(CLK), .Q(r11_q));  // open: clr
  Register #(.width(16)) r12 (.D(data_in), .en(demultiplexer_1_out12), .clk(CLK), .Q(r12_q));  // open: clr
  Register #(.width(16)) r13 (.D(data_in), .en(demultiplexer_1_out13), .clk(CLK), .Q(r13_q));  // open: clr
  Register #(.width(16)) r14 (.D(data_in), .en(demultiplexer_1_out14), .clk(CLK), .Q(r14_q));  // open: clr
  Register #(.width(16)) r15 (.D(data_in), .en(demultiplexer_1_out15), .clk(CLK), .Q(r15_q));  // open: clr
  assign data_out = not_1_out ? multiplexer_4_out : 16'bz;  // Controlled_Buffer controlled_buffer_1
  Multiplexer #(.select(4), .width(16)) multiplexer_4 (
    .in0(r0_out), .in1(r1_out), .in2(r2_q), .in3(r3_q), .in4(r4_q), .in5(r5_q), .in6(r6_q), .in7(r7_q),
    .in8(r8_q), .in9(r9_q), .in10(r10_q), .in11(r11_q), .in12(r12_q), .in13(r13_q), .in14(r14_q),
    .in15(r15_q), .out(multiplexer_4_out), .sel(regid));
  not not_1 (not_1_out, wr_enable);
  assign and_1_out = r0_out[15:8] & r1_out[15:8];  // AND_Gate and_1, 8 bits wide
  or or_2 (BUSY, r0_out[0], r0_out[1], r0_out[2], r0_out[3], r0_out[4], r0_out[5], r0_out[6], r0_out[7]);
  Priority_Encoder priority_encoder_1 (
    .in0(and_1_out[7]), .in1(and_1_out[6]), .in2(and_1_out[5]), .in3(and_1_out[4]), .in4(and_1_out[3]),
    .in5(and_1_out[2]), .in6(and_1_out[1]), .in7(and_1_out[0]), .out(INT_ID), .gs(INT));  // open: en_in, en_out

  // Other names for the same wires on the sheet: data_tunnel[15:0] = data_in; reg_num[3:0] = regid; we = wr_enable

  // Notes on the sheet:
  //   necessary to prevent incredibely rare situation
  //   when int happens EXACTLY on mask update
endmodule

module IO (
  input  CLK,
  input  iint,
  input  [2:0] iintid,
  input  [15:0] iiobus,
  input  [2:0] iioid,
  input  [1:0] iiocmd,
  input  [6:0] ikeychar,
  input  ikeyaval,
  output [15:0] oiobus,
  output [7:0] ointasssert,
  output [7:0] obusyassert,
  output ogpu_clear,
  output okeyread,
  output [15:0] oled
);

  wire and_2_out, and_3_out, and_4_out, and_7_out, and_8_out, and_9_out, and_10_out, demultiplexer_2_out0,
       demultiplexer_2_out1, demultiplexer_2_out2, demultiplexer_2_out3, demultiplexer_2_out4,
       demultiplexer_2_out5, demultiplexer_2_out6, demultiplexer_2_out7, is_iht_mode_q, isboard, isgpu,
       iskeyboard, isled, not_1_out, or_2_out, re, we;
  wire [2:0] register_5_q, register_14_q;
  wire [6:0] keyoutput;
  wire [7:0] multiplexer_1_out;
  wire [11:0] adder_1_out, register_2_q;
  wire [15:0] boardoutput, multiplexer_2_out, register_6_q, register_7_q, register_8_q, register_9_q,
       register_10_q, register_11_q, register_12_q, register_13_q;

  or or_1 (okeyread, and_2_out, and_3_out);
  Register register_1 (.D(multiplexer_1_out), .en(okeyread), .clk(CLK), .Q({ointasssert[6], keyoutput}), .clr(1'b0));
  Multiplexer #(.width(8)) multiplexer_1 (
    .in0({8{1'b0}}), .in1({1'b1, ikeychar}), .out(multiplexer_1_out), .sel(ikeyaval));
  Register #(.width(12)) register_2 (.D(adder_1_out), .en(1'b1), .clk(CLK), .Q(register_2_q), .clr(ointasssert[7]));
  Adder #(.width(12)) adder_1 (.a(register_2_q), .b(12'h1), .out(adder_1_out));  // open: cin, cout
  and and_1 (ogpu_clear, isgpu, we);
  and and_2 (and_2_out, iskeyboard, re);
  and and_3 (and_3_out, ikeyaval, ~ointasssert[6]);  // AND_Gate
  and and_4 (and_4_out, isled, we);
  and and_5 (we, iiocmd[0], iiocmd[1]);
  and and_6 (re, iiocmd[1], ~iiocmd[0]);  // AND_Gate
  Register #(.width(16)) register_3 (.D(iiobus), .en(and_4_out), .clk(CLK), .Q(oled), .clr(1'b0));
  and and_7 (and_7_out, isboard, re);
  Multiplexer #(.select(3), .width(16)) multiplexer_2 (
    .in0(boardoutput), .in1({{9{1'b0}}, keyoutput}), .in2({16{1'b0}}), .in3({16{1'b0}}), .in4({16{1'b0}}),
    .in5({16{1'b0}}), .in6({16{1'b0}}), .in7({16{1'b0}}), .out(multiplexer_2_out), .sel(iioid));
  or or_2 (or_2_out, and_7_out, register_2_q[11]);
  assign oiobus = re ? multiplexer_2_out : 16'bz;  // Controlled_Buffer controlled_buffer_1
  Register #(.width(1)) register_4 (.D(register_2_q[11]), .en(or_2_out), .clk(CLK), .Q(ointasssert[7]), .clr(1'b0));
  Demultiplexer #(.select(3)) demultiplexer_1 (
    .out0(isboard), .out1(iskeyboard), .out2(isgpu), .out7(isled), .in(1'b1), .sel(iioid));  // open: out3, out4, out5, out6
  and and_8 (and_8_out, isboard, we);
  Register #(.width(1)) is_iht_mode (.D(not_1_out), .en(and_8_out), .clk(CLK), .Q(is_iht_mode_q), .clr(1'b0));
  not not_1 (not_1_out, is_iht_mode_q);
  and and_9 (and_9_out, not_1_out, and_8_out);
  and and_10 (and_10_out, and_8_out, is_iht_mode_q);
  Register #(.width(3)) register_5 (.D(iiobus[2:0]), .en(and_9_out), .clk(CLK), .Q(register_5_q), .clr(1'b0));
  Pull_Resistor pull_resistor_1 (.node(register_5_q));
  Demultiplexer #(.select(3)) demultiplexer_2 (
    .out0(demultiplexer_2_out0), .out1(demultiplexer_2_out1), .out2(demultiplexer_2_out2),
    .out3(demultiplexer_2_out3), .out4(demultiplexer_2_out4), .out5(demultiplexer_2_out5),
    .out6(demultiplexer_2_out6), .out7(demultiplexer_2_out7), .in(and_10_out), .sel(register_5_q));
  Register #(.width(16)) register_6 (.D(iiobus), .en(demultiplexer_2_out0), .Q(register_6_q), .clk(CLK), .clr(1'b0));
  Register #(.width(16)) register_7 (.D(iiobus), .en(demultiplexer_2_out1), .Q(register_7_q), .clk(CLK), .clr(1'b0));
  Register #(.width(16)) register_8 (.D(iiobus), .en(demultiplexer_2_out2), .Q(register_8_q), .clk(CLK), .clr(1'b0));
  Register #(.width(16)) register_9 (.D(iiobus), .en(demultiplexer_2_out3), .Q(register_9_q), .clk(CLK), .clr(1'b0));
  Register #(.width(16)) register_10 (.D(iiobus), .en(demultiplexer_2_out4), .Q(register_10_q), .clk(CLK), .clr(1'b0));
  Register #(.width(16)) register_11 (.D(iiobus), .en(demultiplexer_2_out5), .Q(register_11_q), .clk(CLK), .clr(1'b0));
  Register #(.width(16)) register_12 (.D(iiobus), .en(demultiplexer_2_out6), .Q(register_12_q), .clk(CLK), .clr(1'b0));
  Register #(.width(16)) register_13 (.D(iiobus), .en(demultiplexer_2_out7), .Q(register_13_q), .clk(CLK), .clr(1'b0));
  Register #(.width(3)) register_14 (.D(iintid), .en(iint), .clk(CLK), .Q(register_14_q), .clr(1'b0));
  Multiplexer #(.select(3), .width(16)) multiplexer_3 (
    .in0(register_6_q), .in1(register_7_q), .in2(register_8_q), .in3(register_9_q), .in4(register_10_q),
    .in5(register_11_q), .in6(register_12_q), .in7(register_13_q), .out(boardoutput), .sel(register_14_q));

  assign obusyassert = {8{1'b0}};
  assign ointasssert[5:0] = {6{1'b0}};

  // Other names for the same wires on the sheet: keychar[6:0] = ikeychar; int = iint; intind[2:0] = iintid;
  //   iobus[15:0] = iiobus; ioid[2:0] = iioid; keyaval = ikeyaval; keyread = okeyread; key_present = ointasssert[6];
  //   clockint = ointasssert[7]

  // Notes on the sheet:
  //   GPU interface
  //   clock
  //   CPU interface
  //   keyboard interface
  //   led interface
  //   IO interface
  //   board interface
endmodule
