// Logisim project memory_controller.circ as structural Verilog: 1 circuit, main circuit memory_controller
module memory_controller (
  input  [15:0] DataBUSin,
  input  [2:0] MODE,
  output [15:0] DataBUSout
);

  wire and_1_out, and_4_out, and_5_out, clk, output_enable, write_enable;
  wire [15:0] adder_1_out, general_purpose_memory_dout, multiplexer_1_out, multiplexer_2_out, RegAddr_q,
       rom_1_data;

  Clock clock_1 (.out(clk));
  and and_1 (and_1_out, ~MODE[2], MODE[1]);  // AND_Gate
  and and_2 (write_enable, MODE[2], ~MODE[1], ~MODE[0]);  // AND_Gate
  and and_3 (output_enable, MODE[2], ~MODE[1], MODE[0]);  // AND_Gate
  Multiplexer #(.width(16)) multiplexer_1 (.in0(DataBUSin), .in1(adder_1_out), .out(multiplexer_1_out), .sel(MODE[0]));
  Register #(.width(16)) RegAddr (.D(multiplexer_1_out), .en(and_1_out), .clk(clk), .Q(RegAddr_q));  // open: clr
  Adder #(.width(16)) adder_1 (.a(RegAddr_q), .b(16'h1), .out(adder_1_out));  // open: cin, cout
  and and_4 (and_4_out, ~RegAddr_q[15], write_enable);  // AND_Gate
  and and_5 (and_5_out, RegAddr_q[15], write_enable);
  RAM #(.addrWidth(16), .dataWidth(16)) VRAM (
    .addr(RegAddr_q), .we(and_4_out), .oe(1'b0), .clk(clk), .din(DataBUSin));  // open: dout
  ROM #(.addrWidth(16), .dataWidth(16)) rom_1 (.addr(RegAddr_q), .data(rom_1_data));
  RAM #(.addrWidth(16), .dataWidth(16)) general_purpose_memory (
    .addr(RegAddr_q), .we(and_5_out), .oe(1'b1), .clk(clk), .din(DataBUSin),
    .dout(general_purpose_memory_dout));
  Multiplexer #(.width(16)) multiplexer_2 (
    .in0(rom_1_data), .in1(general_purpose_memory_dout), .out(multiplexer_2_out), .sel(RegAddr_q[15]));
  assign DataBUSout = output_enable ? multiplexer_2_out : 16'bz;  // Controlled_Buffer controlled_buffer_1

  // Other names for the same wires on the sheet: Data_in[15:0] = DataBUSin

  // Notes on the sheet:
  //   15 bit
  //   contents of rom_1 (hex, n*v repeats v):
  //   5*0 dead 32707*0 beef 55*0 dead
  //   VRAM
  //   ROM
  //   RAM
endmodule
